// Logisim project cpu21-riscv.circ as structural Verilog: 19 circuits, main circuit ◇单周期RISC-V
module \单周期RISC_V  (
  input  IR1,
  input  IR2,
  input  IR3,
  output RegWrite,
  output MemWrite,
  output [31:0] PC,
  output [31:0] IR,
  output [31:0] RDin,
  output [31:0] MDin,
  output [31:0] LedData
);

  wire and_1_out, and_4_out, and_5_out, and_6_out, BEQ, BGE, BNE, BranchSuccess, Byte, CLK, clock_1_out,
       comparator_1_eq, comparator_2_eq, comparator_3_eq, comparator_3_lt, dipswitch_1_p1, ecall, Equal,
       GEqual, Go, halt, IR1_t, IR2_t, IR3_t, IRA, IRB, IRC, JAL, JALR, nand_1_out, not_1_out, not_2_out,
       not_3_out, not_4_out, not_5_out, or_4_out, or_5_out, RST, URET, W1, W2, W3, \单周期硬布线控制器_1_alu_src ,
       \单周期硬布线控制器_1_memtoreg , \单周期硬布线控制器_1_s_type , \单周期硬布线控制器_1_u_type ;
  wire [1:0] priority_encoder_1_out;
  wire [2:0] priority_encoder_2_out;
  wire [3:0] \单周期硬布线控制器_1_alu_op ;
  wire [4:0] multiplexer_1_out, multiplexer_2_out;
  wire [7:0] multiplexer_6_out;
  wire [11:0] multiplexer_3_out;
  wire [12:0] CNT_num;
  wire [15:0] \总周期数 ;
  wire [31:0] ALUOut, and_3_out, bit_extender_1_out, bit_extender_2_out, bit_extender_3_out, bPC, BreakPoint,
       jalPC, multiplexer_4_out, multiplexer_7_out, NextPC, R1, ram_1_data;

  Button \u_总复位  (.out(RST));
  Button _1 (.out(IRA));
  Button _2 (.out(IRB));
  Button _3 (.out(IRC));
  Button \u_继续运行  (.out(Go));
  LED led_1 (.in(W1));
  LED led_2 (.in(W2));
  LED led_3 (.in(W3));
  Hex_Digit_Display hex_digit_display_1 (.value(LedData[31:28]));  // open: dp
  not not_1 (not_1_out, halt);
  Comparator #(.width(32)) comparator_1 (.a(MDin), .b(32'h22), .eq(comparator_1_eq));  // open: gt, lt
  Hex_Digit_Display hex_digit_display_2 (.value(LedData[27:24]));  // open: dp
  Hex_Digit_Display hex_digit_display_3 (.value(LedData[23:20]));  // open: dp
  Register #(.width(32), .Select("low")) u_PC (.D(NextPC), .en(not_1_out), .Q(PC), .clk(CLK), .clr(RST));
  and and_1 (and_1_out, ecall, comparator_1_eq);
  Hex_Digit_Display hex_digit_display_4 (.value(LedData[15:12]));  // open: dp
  Hex_Digit_Display hex_digit_display_5 (.value(LedData[19:16]));  // open: dp
  Register #(.width(32), .Select("low")) register_1 (.D(R1), .en(and_1_out), .Q(LedData), .clk(CLK), .clr(RST));
  Hex_Digit_Display hex_digit_display_6 (.value(LedData[7:4]));  // open: dp
  Hex_Digit_Display hex_digit_display_7 (.value(LedData[11:8]));  // open: dp
  // Probe on \总周期数 
  // RiscV_Probe riscv_probe_1: pin names not known; wires that end beside it: PC[11:2], IR
  ROM #(.addrWidth(10), .dataWidth(32), .Select("high")) rom_1 (.addr(PC[11:2]), .data(IR));
  Hex_Digit_Display hex_digit_display_8 (.value(LedData[3:0]));  // open: dp
  not not_2 (not_2_out, comparator_1_eq);
  \单周期硬布线控制器  \u_单周期硬布线控制器_1  (
    .Funct({IR[30], IR[25], IR[14:12]}), .OP(IR[6:2]), .ALU_OP(\单周期硬布线控制器_1_alu_op ),
    .MemToReg(\单周期硬布线控制器_1_memtoreg ), .MemWrite(MemWrite), .ALU_SRC(\单周期硬布线控制器_1_alu_src ),
    .RegWrite(RegWrite), .ecall(ecall), .S_type(\单周期硬布线控制器_1_s_type ), .Jalr(JALR), .Beq(BEQ), .JAL(JAL),
    .Bne(BNE), .in_3(IR[21]), .uret(URET), .BGE(BGE), .Byte(Byte), .U_Type(\单周期硬布线控制器_1_u_type ));
  Multiplexer #(.width(5), .enable("false")) multiplexer_1 (
    .in0(IR[19:15]), .in1(5'b01010), .out(multiplexer_1_out), .sel(ecall));
  Multiplexer #(.width(5), .enable("false")) multiplexer_2 (
    .in0(IR[24:20]), .in1(5'b10001), .out(multiplexer_2_out), .sel(ecall));
  not not_3 (not_3_out, Go);
  or or_1 (IR1_t, IR1, IRA);
  Multiplexer #(.width(12), .enable("false")) multiplexer_3 (
    .in0(IR[31:20]), .in1({IR[31:25], IR[11:7]}), .out(multiplexer_3_out), .sel(\单周期硬布线控制器_1_s_type ));
  and and_2 (halt, not_2_out, ecall, not_3_out);
  or or_2 (IR2_t, IR2, IRB);
  assign bit_extender_1_out = {{20{multiplexer_3_out[11]}}, multiplexer_3_out};  // Bit_Extender bit_extender_1
  assign bit_extender_2_out = {{20{IR[7]}}, {IR[7], IR[30:25], IR[11:8], 1'b0}};  // Bit_Extender bit_extender_2
  assign bit_extender_3_out = {{12{IR[19]}}, {IR[19:12], IR[20], IR[30:21], 1'b0}};  // Bit_Extender bit_extender_3
  Regifile regifile_1 (
    .Din(RDin), .Clk(CLK), .R1(R1), .R2(MDin), .WE(RegWrite), .W_num(IR[11:7]), .R1_num(multiplexer_1_out),
    .R2_num(multiplexer_2_out));
  or or_3 (IR3_t, IR3, IRC);
  Multiplexer #(.width(32), .enable("false")) multiplexer_4 (
    .in0(MDin), .in1(bit_extender_1_out), .out(multiplexer_4_out), .sel(\单周期硬布线控制器_1_alu_src ));
  Adder #(.width(32)) adder_1 (.a(PC), .b(bit_extender_2_out), .out(bPC));  // open: cin, cout
  Adder #(.width(32)) adder_2 (.a(PC), .b(bit_extender_3_out), .out(jalPC));  // open: cin, cout
  ALU alu_1 (
    .X(R1), .Y(multiplexer_4_out), .AluOP(\单周期硬布线控制器_1_alu_op ), .Equal(Equal), .Result(ALUOut),
    .out_4(GEqual));  // open: Result_2, out_6
  Register #(.width(32), .Select("low")) register_2 (.D(R1), .en(ecall), .clk(comparator_2_eq), .clr(RST));  // open: Q
  Comparator #(.width(32)) comparator_2 (.a(MDin), .b(32'h22), .eq(comparator_2_eq));  // open: gt, lt
  Multiplexer #(.width(32), .enable("false")) multiplexer_5 (
    .in0(multiplexer_7_out), .in1({{24{1'b0}}, multiplexer_6_out}), .out(RDin), .sel(Byte));
  or or_4 (or_4_out, JALR, JAL);
  RAM #(.addrWidth(10), .dataWidth(32), .bus("separate"), .Select("high"), .simpleMode("false")) ram_1 (
    .addr(ALUOut[11:2]), .din(MDin), .data(ram_1_data), .str(MemWrite), .clk(CLK));  // open: sel, ld, clr
  Multiplexer #(.select(2), .width(8), .enable("false")) multiplexer_6 (
    .in0(multiplexer_7_out[7:0]), .in1(multiplexer_7_out[15:8]), .in2(multiplexer_7_out[23:16]),
    .in3(multiplexer_7_out[31:24]), .out(multiplexer_6_out), .sel(ALUOut[1:0]));
  not not_4 (not_4_out, comparator_2_eq);
  Priority_Encoder #(.select(2)) priority_encoder_1 (
    .in0(1'b1), .in1(\单周期硬布线控制器_1_memtoreg ), .in2(or_4_out), .in3(\单周期硬布线控制器_1_u_type ),
    .out(priority_encoder_1_out));  // open: gs, en_out, en_in
  Multiplexer #(.select(2), .width(32), .enable("false")) multiplexer_7 (
    .in0(ALUOut), .in1(ram_1_data), .in2(BreakPoint), .in3({IR[31:12], {12{1'b0}}}), .out(multiplexer_7_out),
    .sel(priority_encoder_1_out));
  or or_5 (or_5_out, RST, Go);
  D_Flip_Flop d_ff_1 (.clk(not_4_out), .D(ecall), .reset(or_5_out));  // open: Q, Qn, preset
  // DipSwitch #(.NSwitches(1)) dipswitch_1: pin names not known; wires that end beside it: dipswitch_1_p1
  // Probe on 13'h609
  Comparator #(.width(13)) comparator_3 (
    .a(CNT_num), .b(13'h609), .eq(comparator_3_eq), .lt(comparator_3_lt));  // open: gt
  Clock clock_1 (.out(clock_1_out));
  nand nand_1 (nand_1_out, dipswitch_1_p1, comparator_3_eq);
  Counter #(.width(13), .max('h1fff), .ongoal("stay"), .behavior("old")) counter_1 (
    .count(comparator_3_lt), .Q(CNT_num), .clk(clock_1_out));  // open: load, D, carry, clr, preset
  assign CLK = nand_1_out ? clock_1_out : 1'bz;  // Controlled_Buffer controlled_buffer_1
  not not_5 (not_5_out, Equal);
  Pull_Resistor #(.pull(1)) pull_resistor_1 (.node(CLK));
  Adder #(.width(32)) adder_3 (.a(PC), .b(32'h4), .out(BreakPoint));  // open: cin, cout
  assign and_3_out = ALUOut & 32'hfffffffe;  // AND_Gate and_3, 32 bits wide
  and and_4 (and_4_out, BNE, not_5_out);
  and and_5 (and_5_out, BEQ, Equal);
  and and_6 (and_6_out, BGE, GEqual);
  or or_6 (BranchSuccess, and_4_out, and_5_out, and_6_out);
  Priority_Encoder priority_encoder_2 (
    .in0(1'b1), .in1(BranchSuccess), .in2(JAL), .in3(JALR), .in4(URET), .in5(1'b0), .in6(1'b0), .in7(1'b0),
    .out(priority_encoder_2_out));  // open: gs, en_out, en_in
  Multiplexer #(.select(3), .width(32), .enable("false")) multiplexer_8 (
    .in0(BreakPoint), .in1(bPC), .in2(jalPC), .in3(and_3_out), .out(NextPC), .sel(priority_encoder_2_out));  // open: in4, in5, in6, in7

  // Other names for the same wires on the sheet: CurrentPC[31:0] = PC; R2[31:0] = MDin; UImm[31:12] = IR[31:12]

  // Notes on the sheet:
  //   中断源
  //   中断等待指示
  //   数据通路
  //   LED显示&halt控制
  //   数码管输出应该用寄存器锁存，否则显示数据只能一闪而过
  //   数码管输出
  //   指令探针
  //   指令存储器
  //   contents of rom_1 (hex, n*v repeats v):
  //   313 1000e13 8400493 849493 8348493 400913 891913 490913 849493 8248493 849493 8148493 891913 490913
  //   891913 490913 932023 12484b3 430313 fffe0e13 fe0e18e3 2000e13 313 34483 900533 2200893 73 130313
  //   fffe0e13 fe0e14e3 a00893 73
  //   指令字
  //   JAL
  //   JALR
  //   URET
  //   BGE
  //   Byte
  //   IType-Imm
  //   SType-Imm
  //   BType-Imm
  //   JType-Imm
  //   UType-Imm
  //   Beq
  //   Bne
  //   MemToReg
  //   MemWrite
  //   AluOP
  //   AluSrcB
  //   RegWrite
  //   UType
  //   SType
  //   异步废稿
  //   为方便自动评测，需要输出PC，IR，寄存器堆写如数据RDin
  //   数据存储器
  //   RAM写使能MemWrite、RAM写入数据MDin等信号
  //   控制位
  //   暂停节拍，不能为0
  //   戳工具置1进入计数暂停模式，ctrl+k时钟自动运行到对应节拍暂停
  //   ctrl+k关闭时钟连续运行，将控制位置零，进入单步调试模式调试
  //   用这个时钟源需要去掉电路中的其他时钟源
  //   跳转处理电路
  //   可计数暂停的时钟源
endmodule

// 单周期硬布线控制器
module \单周期硬布线控制器  (
  input  [4:0] OP,
  input  [4:0] Funct,
  input  in_3,
  output [3:0] ALU_OP,
  output uret,
  output MemToReg,
  output ecall,
  output MemWrite,
  output ALU_SRC,
  output Byte,
  output U_Type,
  output RegWrite,
  output S_type,
  output Beq,
  output Bne,
  output Jalr,
  output JAL,
  output BGE
);

  wire \控制信号自动生成_1_ecall ;

  \运算控制器自动生成  \u_运算控制器自动生成_1  (
    .OP2(OP[0]), .OP3(OP[1]), .OP4(OP[2]), .OP5(OP[3]), .OP6(OP[4]), .F12(Funct[0]), .F13(Funct[1]),
    .F14(Funct[2]), .F25(Funct[3]), .F30(Funct[4]), .S0(ALU_OP[0]), .S1(ALU_OP[1]), .S2(ALU_OP[2]),
    .S3(ALU_OP[3]));
  \控制信号自动生成  \u_控制信号自动生成_1  (
    .OP2(OP[0]), .OP3(OP[1]), .OP4(OP[2]), .OP5(OP[3]), .MemToReg(MemToReg), .OP6(OP[4]), .F12(Funct[0]),
    .F13(Funct[1]), .F14(Funct[2]), .F25(Funct[3]), .F30(Funct[4]), .MemWrite(MemWrite), .ALU_SRC(ALU_SRC),
    .Byte(Byte), .U_Type(U_Type), .RegWrite(RegWrite), .ecall(\控制信号自动生成_1_ecall ), .S_Type(S_type),
    .BEQ(Beq), .BNE(Bne), .JALR(Jalr), .JAL(JAL), .BGE(BGE));
  and and_1 (uret, in_3, \控制信号自动生成_1_ecall );
  and and_2 (ecall, ~in_3, \控制信号自动生成_1_ecall );  // AND_Gate

  // Other names for the same wires on the sheet: IR21 = in_3; OP_CODE[4:0] = OP

  // Notes on the sheet:
  //   运算器控制器，根据指令生成运算器功能选择信号
  //   控制信号生成，产生数据通路需要的其他控制信号
endmodule

// 运算器控制器
module \运算控制器自动生成  (
  input  OP2,
  input  OP3,
  input  OP4,
  input  OP5,
  input  OP6,
  input  F12,
  input  F13,
  input  F14,
  input  F25,
  input  F30,
  output S0,
  output S1,
  output S2,
  output S3
);

  wire and_1_out, and_2_out, and_3_out, and_4_out, and_5_out, and_6_out, and_7_out, and_8_out, and_9_out,
       and_10_out, and_11_out, and_12_out, and_13_out, and_14_out, and_15_out, and_16_out, and_17_out,
       and_18_out, and_19_out, and_20_out, and_21_out, and_22_out, and_23_out, and_24_out, and_25_out,
       and_26_out, and_27_out, and_28_out, and_29_out, and_30_out, and_31_out, and_32_out, and_33_out,
       and_34_out, and_35_out, and_36_out, and_37_out, and_38_out, and_39_out, and_40_out, not_1_out,
       not_2_out, not_3_out, not_4_out, not_5_out, not_6_out, not_7_out, not_8_out, not_9_out, not_10_out,
       not_11_out, not_12_out, not_13_out, not_14_out, not_15_out, not_16_out, not_17_out, not_18_out,
       not_19_out, not_20_out, not_21_out, not_22_out, not_23_out, not_24_out, not_25_out, not_26_out,
       not_27_out, not_28_out, not_29_out, not_30_out, not_31_out, not_32_out, not_33_out, not_34_out,
       not_35_out, not_36_out, not_37_out, not_38_out, not_39_out, not_40_out, not_41_out, not_42_out,
       not_43_out, not_44_out, not_45_out, not_46_out, not_47_out, not_48_out, not_49_out, not_50_out,
       not_51_out, not_52_out, not_53_out, not_54_out, not_55_out, not_56_out, not_57_out, not_58_out,
       not_59_out, not_60_out, not_61_out, not_62_out, not_63_out, not_64_out, not_65_out, not_66_out,
       not_67_out, not_68_out, not_69_out, not_70_out, not_71_out, not_72_out, not_73_out, not_74_out,
       not_75_out, not_76_out, not_77_out, not_78_out, not_79_out, not_80_out, not_81_out, not_82_out,
       not_83_out, not_84_out, not_85_out, not_86_out, not_87_out, not_88_out, not_89_out, not_90_out,
       not_91_out, not_92_out, not_93_out, not_94_out, not_95_out, not_96_out, not_97_out, not_98_out,
       not_99_out, not_100_out, not_101_out, not_102_out, not_103_out, not_104_out, not_105_out, not_106_out,
       not_107_out, not_108_out, not_109_out, not_110_out, not_111_out, not_112_out, not_113_out,
       not_114_out, not_115_out, not_116_out, not_117_out, not_118_out, not_119_out, not_120_out,
       not_121_out, not_122_out, not_123_out, not_124_out, not_125_out, not_126_out, not_127_out,
       not_128_out, not_129_out, not_130_out, not_131_out, not_132_out, not_133_out, not_134_out,
       not_135_out, not_136_out, not_137_out, not_138_out, not_139_out, not_140_out, not_141_out,
       not_142_out, not_143_out, not_144_out, not_145_out, not_146_out, not_147_out, not_148_out,
       not_149_out, not_150_out, not_151_out, not_152_out, not_153_out, not_154_out, not_155_out,
       not_156_out, not_157_out, not_158_out, not_159_out, not_160_out, not_161_out, not_162_out,
       not_163_out, not_164_out, not_165_out, not_166_out, not_167_out, not_168_out, not_169_out,
       not_170_out, not_171_out, not_172_out, not_173_out, not_174_out, not_175_out, not_176_out,
       not_177_out, not_178_out, not_179_out, not_180_out, not_181_out, not_182_out, not_183_out,
       not_184_out, not_185_out, not_186_out, not_187_out, not_188_out, not_189_out, not_190_out,
       not_191_out, not_192_out, not_193_out, not_194_out, not_195_out, not_196_out, not_197_out,
       not_198_out, not_199_out, not_200_out, not_201_out, not_202_out, not_203_out, not_204_out,
       not_205_out, not_206_out, not_207_out, not_208_out, not_209_out, not_210_out, not_211_out,
       not_212_out, not_213_out, not_214_out, not_215_out, not_216_out, not_217_out, not_218_out,
       not_219_out, not_220_out, not_221_out, not_222_out, not_223_out, not_224_out, not_225_out,
       not_226_out, not_227_out, not_228_out, not_229_out, not_230_out, not_231_out, not_232_out,
       not_233_out, not_234_out, not_235_out, not_236_out, not_237_out, not_238_out;

  not not_1 (not_1_out, F30);
  not not_2 (not_2_out, F25);
  not not_3 (not_3_out, F14);
  not not_4 (not_4_out, F13);
  not not_5 (not_5_out, F12);
  not not_6 (not_6_out, OP6);
  not not_7 (not_7_out, OP3);
  not not_8 (not_8_out, OP2);
  not not_9 (not_9_out, F30);
  not not_10 (not_10_out, F25);
  not not_11 (not_11_out, OP6);
  not not_12 (not_12_out, OP3);
  not not_13 (not_13_out, OP2);
  not not_14 (not_14_out, F30);
  not not_15 (not_15_out, F25);
  not not_16 (not_16_out, F14);
  not not_17 (not_17_out, F12);
  not not_18 (not_18_out, OP6);
  not not_19 (not_19_out, OP3);
  not not_20 (not_20_out, OP2);
  not not_21 (not_21_out, F14);
  not not_22 (not_22_out, F13);
  not not_23 (not_23_out, F12);
  not not_24 (not_24_out, OP6);
  not not_25 (not_25_out, OP5);
  not not_26 (not_26_out, OP3);
  not not_27 (not_27_out, OP2);
  not not_28 (not_28_out, OP6);
  not not_29 (not_29_out, OP5);
  not not_30 (not_30_out, OP3);
  not not_31 (not_31_out, OP2);
  not not_32 (not_32_out, F13);
  not not_33 (not_33_out, F12);
  not not_34 (not_34_out, OP6);
  not not_35 (not_35_out, OP5);
  not not_36 (not_36_out, OP3);
  not not_37 (not_37_out, OP2);
  not not_38 (not_38_out, F14);
  not not_39 (not_39_out, F12);
  not not_40 (not_40_out, OP6);
  not not_41 (not_41_out, OP5);
  not not_42 (not_42_out, OP3);
  not not_43 (not_43_out, OP2);
  not not_44 (not_44_out, F25);
  not not_45 (not_45_out, F13);
  not not_46 (not_46_out, OP6);
  not not_47 (not_47_out, OP5);
  not not_48 (not_48_out, OP3);
  not not_49 (not_49_out, OP2);
  not not_50 (not_50_out, F14);
  not not_51 (not_51_out, F12);
  not not_52 (not_52_out, OP6);
  not not_53 (not_53_out, OP5);
  not not_54 (not_54_out, OP4);
  not not_55 (not_55_out, OP3);
  not not_56 (not_56_out, OP2);
  not not_57 (not_57_out, F14);
  not not_58 (not_58_out, F12);
  not not_59 (not_59_out, OP6);
  not not_60 (not_60_out, OP4);
  not not_61 (not_61_out, OP3);
  not not_62 (not_62_out, OP2);
  not not_63 (not_63_out, F14);
  not not_64 (not_64_out, F13);
  not not_65 (not_65_out, F12);
  not not_66 (not_66_out, OP4);
  not not_67 (not_67_out, OP3);
  not not_68 (not_68_out, OP2);
  not not_69 (not_69_out, F14);
  not not_70 (not_70_out, F13);
  not not_71 (not_71_out, OP4);
  not not_72 (not_72_out, OP3);
  not not_73 (not_73_out, OP2);
  not not_74 (not_74_out, OP4);
  not not_75 (not_75_out, OP3);
  not not_76 (not_76_out, F30);
  not not_77 (not_77_out, F25);
  not not_78 (not_78_out, F13);
  not not_79 (not_79_out, F12);
  not not_80 (not_80_out, OP6);
  not not_81 (not_81_out, OP3);
  not not_82 (not_82_out, OP2);
  not not_83 (not_83_out, F13);
  not not_84 (not_84_out, F12);
  not not_85 (not_85_out, OP6);
  not not_86 (not_86_out, OP5);
  not not_87 (not_87_out, OP4);
  not not_88 (not_88_out, OP3);
  not not_89 (not_89_out, OP2);
  not not_90 (not_90_out, F25);
  not not_91 (not_91_out, F14);
  not not_92 (not_92_out, F13);
  not not_93 (not_93_out, F12);
  not not_94 (not_94_out, OP6);
  not not_95 (not_95_out, OP3);
  not not_96 (not_96_out, OP2);
  not not_97 (not_97_out, F30);
  not not_98 (not_98_out, F25);
  not not_99 (not_99_out, OP6);
  not not_100 (not_100_out, OP3);
  not not_101 (not_101_out, OP2);
  not not_102 (not_102_out, F30);
  not not_103 (not_103_out, F25);
  not not_104 (not_104_out, F14);
  not not_105 (not_105_out, F12);
  not not_106 (not_106_out, OP6);
  not not_107 (not_107_out, OP3);
  not not_108 (not_108_out, OP2);
  not not_109 (not_109_out, OP6);
  not not_110 (not_110_out, OP5);
  not not_111 (not_111_out, OP3);
  not not_112 (not_112_out, OP2);
  not not_113 (not_113_out, F14);
  not not_114 (not_114_out, F12);
  not not_115 (not_115_out, OP6);
  not not_116 (not_116_out, OP5);
  not not_117 (not_117_out, OP3);
  not not_118 (not_118_out, OP2);
  not not_119 (not_119_out, F30);
  not not_120 (not_120_out, F25);
  not not_121 (not_121_out, F13);
  not not_122 (not_122_out, OP6);
  not not_123 (not_123_out, OP5);
  not not_124 (not_124_out, OP3);
  not not_125 (not_125_out, OP2);
  not not_126 (not_126_out, F30);
  not not_127 (not_127_out, F25);
  not not_128 (not_128_out, F14);
  not not_129 (not_129_out, F13);
  not not_130 (not_130_out, F12);
  not not_131 (not_131_out, OP6);
  not not_132 (not_132_out, OP3);
  not not_133 (not_133_out, OP2);
  not not_134 (not_134_out, F25);
  not not_135 (not_135_out, F14);
  not not_136 (not_136_out, F13);
  not not_137 (not_137_out, F12);
  not not_138 (not_138_out, OP6);
  not not_139 (not_139_out, OP3);
  not not_140 (not_140_out, OP2);
  not not_141 (not_141_out, F30);
  not not_142 (not_142_out, F25);
  not not_143 (not_143_out, OP6);
  not not_144 (not_144_out, OP3);
  not not_145 (not_145_out, OP2);
  not not_146 (not_146_out, F30);
  not not_147 (not_147_out, F25);
  not not_148 (not_148_out, F14);
  not not_149 (not_149_out, OP6);
  not not_150 (not_150_out, OP3);
  not not_151 (not_151_out, OP2);
  not not_152 (not_152_out, F14);
  not not_153 (not_153_out, F13);
  not not_154 (not_154_out, F12);
  not not_155 (not_155_out, OP6);
  not not_156 (not_156_out, OP5);
  not not_157 (not_157_out, OP3);
  not not_158 (not_158_out, OP2);
  not not_159 (not_159_out, OP6);
  not not_160 (not_160_out, OP5);
  not not_161 (not_161_out, OP3);
  not not_162 (not_162_out, OP2);
  not not_163 (not_163_out, F14);
  not not_164 (not_164_out, F12);
  not not_165 (not_165_out, OP6);
  not not_166 (not_166_out, OP5);
  not not_167 (not_167_out, OP4);
  not not_168 (not_168_out, OP3);
  not not_169 (not_169_out, OP2);
  not not_170 (not_170_out, F14);
  not not_171 (not_171_out, F12);
  not not_172 (not_172_out, OP6);
  not not_173 (not_173_out, OP4);
  not not_174 (not_174_out, OP3);
  not not_175 (not_175_out, OP2);
  not not_176 (not_176_out, F14);
  not not_177 (not_177_out, F13);
  not not_178 (not_178_out, F12);
  not not_179 (not_179_out, OP4);
  not not_180 (not_180_out, OP3);
  not not_181 (not_181_out, OP2);
  not not_182 (not_182_out, F14);
  not not_183 (not_183_out, F13);
  not not_184 (not_184_out, OP4);
  not not_185 (not_185_out, OP3);
  not not_186 (not_186_out, OP2);
  not not_187 (not_187_out, OP4);
  not not_188 (not_188_out, OP3);
  not not_189 (not_189_out, F13);
  not not_190 (not_190_out, F12);
  not not_191 (not_191_out, OP6);
  not not_192 (not_192_out, OP5);
  not not_193 (not_193_out, OP4);
  not not_194 (not_194_out, OP3);
  not not_195 (not_195_out, OP2);
  not not_196 (not_196_out, F30);
  not not_197 (not_197_out, F25);
  not not_198 (not_198_out, F12);
  not not_199 (not_199_out, OP6);
  not not_200 (not_200_out, OP3);
  not not_201 (not_201_out, OP2);
  not not_202 (not_202_out, F30);
  not not_203 (not_203_out, F25);
  not not_204 (not_204_out, F14);
  not not_205 (not_205_out, F12);
  not not_206 (not_206_out, OP6);
  not not_207 (not_207_out, OP3);
  not not_208 (not_208_out, OP2);
  not not_209 (not_209_out, F30);
  not not_210 (not_210_out, F25);
  not not_211 (not_211_out, F14);
  not not_212 (not_212_out, OP6);
  not not_213 (not_213_out, OP3);
  not not_214 (not_214_out, OP2);
  not not_215 (not_215_out, F12);
  not not_216 (not_216_out, OP6);
  not not_217 (not_217_out, OP5);
  not not_218 (not_218_out, OP3);
  not not_219 (not_219_out, OP2);
  not not_220 (not_220_out, F13);
  not not_221 (not_221_out, F12);
  not not_222 (not_222_out, OP6);
  not not_223 (not_223_out, OP5);
  not not_224 (not_224_out, OP3);
  not not_225 (not_225_out, OP2);
  not not_226 (not_226_out, F14);
  not not_227 (not_227_out, F12);
  not not_228 (not_228_out, OP6);
  not not_229 (not_229_out, OP5);
  not not_230 (not_230_out, OP3);
  not not_231 (not_231_out, OP2);
  not not_232 (not_232_out, F30);
  not not_233 (not_233_out, F25);
  not not_234 (not_234_out, F13);
  not not_235 (not_235_out, F12);
  not not_236 (not_236_out, OP6);
  not not_237 (not_237_out, OP3);
  not not_238 (not_238_out, OP2);
  and and_1 (and_1_out, not_1_out, not_2_out, not_3_out, not_4_out, not_5_out, not_6_out, OP5, OP4, not_7_out, not_8_out);
  and and_2 (and_2_out, not_9_out, not_10_out, F14, F13, F12, not_11_out, OP5, OP4, not_12_out, not_13_out);
  and and_3 (and_3_out, not_14_out, not_15_out, not_16_out, F13, not_17_out, not_18_out, OP5, OP4, not_19_out, not_20_out);
  and and_4 (and_4_out, not_21_out, not_22_out, not_23_out, not_24_out, not_25_out, OP4, not_26_out, not_27_out);
  and and_5 (and_5_out, F14, F13, F12, not_28_out, not_29_out, OP4, not_30_out, not_31_out);
  and and_6 (and_6_out, F14, not_32_out, not_33_out, not_34_out, not_35_out, OP4, not_36_out, not_37_out);
  and and_7 (and_7_out, not_38_out, F13, not_39_out, not_40_out, not_41_out, OP4, not_42_out, not_43_out);
  and and_8 (and_8_out, F30, not_44_out, F14, not_45_out, F12, not_46_out, not_47_out, OP4, not_48_out, not_49_out);
  and and_9 (and_9_out, not_50_out, F13, not_51_out, not_52_out, not_53_out, not_54_out, not_55_out, not_56_out);
  and and_10 (and_10_out, not_57_out, F13, not_58_out, not_59_out, OP5, not_60_out, not_61_out, not_62_out);
  and and_11 (and_11_out, not_63_out, not_64_out, not_65_out, OP6, OP5, not_66_out, not_67_out, not_68_out);
  and and_12 (and_12_out, not_69_out, not_70_out, F12, OP6, OP5, not_71_out, not_72_out, not_73_out);
  and and_13 (and_13_out, OP6, OP5, not_74_out, not_75_out, OP2);
  and and_14 (and_14_out, not_76_out, not_77_out, F14, not_78_out, not_79_out, not_80_out, OP5, OP4, not_81_out, not_82_out);
  and and_15 (and_15_out, F14, not_83_out, not_84_out, not_85_out, not_86_out, not_87_out, not_88_out, not_89_out);
  and and_16 (and_16_out, F30, not_90_out, not_91_out, not_92_out, not_93_out, not_94_out, OP5, OP4, not_95_out, not_96_out);
  and and_17 (and_17_out, not_97_out, not_98_out, F14, F13, F12, not_99_out, OP5, OP4, not_100_out, not_101_out);
  and and_18 (and_18_out, not_102_out, not_103_out, not_104_out, F13, not_105_out, not_106_out, OP5, OP4, not_107_out, not_108_out);
  and and_19 (and_19_out, F14, F13, F12, not_109_out, not_110_out, OP4, not_111_out, not_112_out);
  and and_20 (and_20_out, not_113_out, F13, not_114_out, not_115_out, not_116_out, OP4, not_117_out, not_118_out);
  and and_21 (and_21_out, not_119_out, not_120_out, F14, not_121_out, F12, not_122_out, not_123_out, OP4, not_124_out, not_125_out);
  and and_22 (and_22_out, not_126_out, not_127_out, not_128_out, not_129_out, not_130_out, not_131_out, OP5, OP4, not_132_out, not_133_out);
  and and_23 (and_23_out, F30, not_134_out, not_135_out, not_136_out, not_137_out, not_138_out, OP5, OP4, not_139_out, not_140_out);
  and and_24 (and_24_out, not_141_out, not_142_out, F14, F13, F12, not_143_out, OP5, OP4, not_144_out, not_145_out);
  and and_25 (and_25_out, not_146_out, not_147_out, not_148_out, F13, F12, not_149_out, OP5, OP4, not_150_out, not_151_out);
  and and_26 (and_26_out, not_152_out, not_153_out, not_154_out, not_155_out, not_156_out, OP4, not_157_out, not_158_out);
  and and_27 (and_27_out, F14, F13, F12, not_159_out, not_160_out, OP4, not_161_out, not_162_out);
  and and_28 (and_28_out, not_163_out, F13, not_164_out, not_165_out, not_166_out, not_167_out, not_168_out, not_169_out);
  and and_29 (and_29_out, not_170_out, F13, not_171_out, not_172_out, OP5, not_173_out, not_174_out, not_175_out);
  and and_30 (and_30_out, not_176_out, not_177_out, not_178_out, OP6, OP5, not_179_out, not_180_out, not_181_out);
  and and_31 (and_31_out, not_182_out, not_183_out, F12, OP6, OP5, not_184_out, not_185_out, not_186_out);
  and and_32 (and_32_out, OP6, OP5, not_187_out, not_188_out, OP2);
  and and_33 (and_33_out, F14, not_189_out, not_190_out, not_191_out, not_192_out, not_193_out, not_194_out, not_195_out);
  and and_34 (and_34_out, not_196_out, not_197_out, F14, F13, not_198_out, not_199_out, OP5, OP4, not_200_out, not_201_out);
  and and_35 (and_35_out, not_202_out, not_203_out, not_204_out, F13, not_205_out, not_206_out, OP5, OP4, not_207_out, not_208_out);
  and and_36 (and_36_out, not_209_out, not_210_out, not_211_out, F13, F12, not_212_out, OP5, OP4, not_213_out, not_214_out);
  and and_37 (and_37_out, F14, F13, not_215_out, not_216_out, not_217_out, OP4, not_218_out, not_219_out);
  and and_38 (and_38_out, F14, not_220_out, not_221_out, not_222_out, not_223_out, OP4, not_224_out, not_225_out);
  and and_39 (and_39_out, not_226_out, F13, not_227_out, not_228_out, not_229_out, OP4, not_230_out, not_231_out);
  and and_40 (and_40_out, not_232_out, not_233_out, F14, not_234_out, not_235_out, not_236_out, OP5, OP4, not_237_out, not_238_out);
  or or_1 (S0, and_1_out, and_2_out, and_3_out, and_4_out, and_5_out, and_6_out, and_7_out, and_8_out, and_9_out, and_10_out, and_11_out, and_12_out, and_13_out, and_14_out, and_15_out);
  or or_2 (S1, and_16_out, and_17_out, and_18_out, and_19_out, and_20_out, and_21_out);
  or or_3 (S2, and_22_out, and_23_out, and_24_out, and_25_out, and_26_out, and_27_out, and_28_out, and_29_out, and_30_out, and_31_out, and_32_out, and_33_out);
  or or_4 (S3, and_34_out, and_35_out, and_36_out, and_37_out, and_38_out, and_39_out, and_40_out);
endmodule

// 控制信号生成
module \控制信号自动生成  (
  input  OP2,
  input  OP3,
  input  OP4,
  input  OP5,
  input  OP6,
  input  F12,
  input  F13,
  input  F14,
  input  F25,
  input  F30,
  output MemToReg,
  output MemWrite,
  output ALU_SRC,
  output Byte,
  output U_Type,
  output RegWrite,
  output ecall,
  output S_Type,
  output BEQ,
  output BNE,
  output JALR,
  output JAL,
  output BGE
);

  wire and_1_out, and_2_out, and_4_out, and_5_out, and_6_out, and_7_out, and_8_out, and_9_out, and_10_out,
       and_11_out, and_12_out, and_13_out, and_14_out, and_17_out, and_18_out, and_19_out, and_20_out,
       and_21_out, and_22_out, and_23_out, and_24_out, and_25_out, and_26_out, and_27_out, and_28_out,
       and_29_out, and_30_out, and_31_out, and_32_out, and_33_out, and_34_out, and_35_out, and_36_out,
       and_37_out, and_38_out, not_1_out, not_2_out, not_3_out, not_4_out, not_5_out, not_6_out, not_7_out,
       not_8_out, not_9_out, not_10_out, not_11_out, not_12_out, not_13_out, not_14_out, not_15_out,
       not_16_out, not_17_out, not_18_out, not_19_out, not_20_out, not_21_out, not_22_out, not_23_out,
       not_24_out, not_25_out, not_26_out, not_27_out, not_28_out, not_29_out, not_30_out, not_31_out,
       not_32_out, not_33_out, not_34_out, not_35_out, not_36_out, not_37_out, not_38_out, not_39_out,
       not_40_out, not_41_out, not_42_out, not_43_out, not_44_out, not_45_out, not_46_out, not_47_out,
       not_48_out, not_49_out, not_50_out, not_51_out, not_52_out, not_53_out, not_54_out, not_55_out,
       not_56_out, not_57_out, not_58_out, not_59_out, not_60_out, not_61_out, not_62_out, not_63_out,
       not_64_out, not_65_out, not_66_out, not_67_out, not_68_out, not_69_out, not_70_out, not_71_out,
       not_72_out, not_73_out, not_74_out, not_75_out, not_76_out, not_77_out, not_78_out, not_79_out,
       not_80_out, not_81_out, not_82_out, not_83_out, not_84_out, not_85_out, not_86_out, not_87_out,
       not_88_out, not_89_out, not_90_out, not_91_out, not_92_out, not_93_out, not_94_out, not_95_out,
       not_96_out, not_97_out, not_98_out, not_99_out, not_100_out, not_101_out, not_102_out, not_103_out,
       not_104_out, not_105_out, not_106_out, not_107_out, not_108_out, not_109_out, not_110_out,
       not_111_out, not_112_out, not_113_out, not_114_out, not_115_out, not_116_out, not_117_out,
       not_118_out, not_119_out, not_120_out, not_121_out, not_122_out, not_123_out, not_124_out,
       not_125_out, not_126_out, not_127_out, not_128_out, not_129_out, not_130_out, not_131_out,
       not_132_out, not_133_out, not_134_out, not_135_out, not_136_out, not_137_out, not_138_out,
       not_139_out, not_140_out, not_141_out, not_142_out, not_143_out, not_144_out, not_145_out,
       not_146_out, not_147_out, not_148_out, not_149_out, not_150_out, not_151_out, not_152_out,
       not_153_out, not_154_out, not_155_out, not_156_out, not_157_out, not_158_out, not_159_out,
       not_160_out, not_161_out, not_162_out, not_163_out, not_164_out, not_165_out, not_166_out,
       not_167_out, not_168_out, not_169_out, not_170_out, not_171_out, not_172_out, not_173_out,
       not_174_out, not_175_out, not_176_out, not_177_out, not_178_out, not_179_out, not_180_out,
       not_181_out, not_182_out, not_183_out, not_184_out, not_185_out, not_186_out, not_187_out,
       not_188_out, not_189_out, not_190_out, not_191_out, not_192_out, not_193_out, not_194_out,
       not_195_out, not_196_out, not_197_out, not_198_out, not_199_out, not_200_out, not_201_out,
       not_202_out, not_203_out, not_204_out, not_205_out, not_206_out, not_207_out, not_208_out,
       not_209_out, not_210_out, not_211_out, not_212_out, not_213_out, not_214_out, not_215_out,
       not_216_out, not_217_out, not_218_out, not_219_out, not_220_out, not_221_out, not_222_out,
       not_223_out, not_224_out, not_225_out, not_226_out, not_227_out, not_228_out, not_229_out,
       not_230_out, not_231_out, not_232_out, not_233_out, not_234_out, not_235_out, not_236_out,
       not_237_out, not_238_out, not_239_out, not_240_out, not_241_out, not_242_out, not_243_out;

  not not_1 (not_1_out, F14);
  not not_2 (not_2_out, F12);
  not not_3 (not_3_out, OP6);
  not not_4 (not_4_out, OP5);
  not not_5 (not_5_out, OP4);
  not not_6 (not_6_out, OP3);
  not not_7 (not_7_out, OP2);
  not not_8 (not_8_out, F13);
  not not_9 (not_9_out, F12);
  not not_10 (not_10_out, OP6);
  not not_11 (not_11_out, OP5);
  not not_12 (not_12_out, OP4);
  not not_13 (not_13_out, OP3);
  not not_14 (not_14_out, OP2);
  not not_15 (not_15_out, F14);
  not not_16 (not_16_out, F12);
  not not_17 (not_17_out, OP6);
  not not_18 (not_18_out, OP4);
  not not_19 (not_19_out, OP3);
  not not_20 (not_20_out, OP2);
  not not_21 (not_21_out, F14);
  not not_22 (not_22_out, F13);
  not not_23 (not_23_out, F12);
  not not_24 (not_24_out, OP6);
  not not_25 (not_25_out, OP5);
  not not_26 (not_26_out, OP3);
  not not_27 (not_27_out, OP2);
  not not_28 (not_28_out, OP6);
  not not_29 (not_29_out, OP5);
  not not_30 (not_30_out, OP3);
  not not_31 (not_31_out, OP2);
  not not_32 (not_32_out, F12);
  not not_33 (not_33_out, OP6);
  not not_34 (not_34_out, OP5);
  not not_35 (not_35_out, OP3);
  not not_36 (not_36_out, OP2);
  not not_37 (not_37_out, F13);
  not not_38 (not_38_out, F12);
  not not_39 (not_39_out, OP6);
  not not_40 (not_40_out, OP5);
  not not_41 (not_41_out, OP3);
  not not_42 (not_42_out, OP2);
  not not_43 (not_43_out, F14);
  not not_44 (not_44_out, F12);
  not not_45 (not_45_out, OP6);
  not not_46 (not_46_out, OP5);
  not not_47 (not_47_out, OP3);
  not not_48 (not_48_out, OP2);
  not not_49 (not_49_out, F30);
  not not_50 (not_50_out, F25);
  not not_51 (not_51_out, F14);
  not not_52 (not_52_out, F13);
  not not_53 (not_53_out, OP6);
  not not_54 (not_54_out, OP5);
  not not_55 (not_55_out, OP3);
  not not_56 (not_56_out, OP2);
  not not_57 (not_57_out, F30);
  not not_58 (not_58_out, F25);
  not not_59 (not_59_out, F13);
  not not_60 (not_60_out, OP6);
  not not_61 (not_61_out, OP5);
  not not_62 (not_62_out, OP3);
  not not_63 (not_63_out, OP2);
  not not_64 (not_64_out, F25);
  not not_65 (not_65_out, F13);
  not not_66 (not_66_out, OP6);
  not not_67 (not_67_out, OP5);
  not not_68 (not_68_out, OP3);
  not not_69 (not_69_out, OP2);
  not not_70 (not_70_out, F14);
  not not_71 (not_71_out, F12);
  not not_72 (not_72_out, OP6);
  not not_73 (not_73_out, OP5);
  not not_74 (not_74_out, OP4);
  not not_75 (not_75_out, OP3);
  not not_76 (not_76_out, OP2);
  not not_77 (not_77_out, F14);
  not not_78 (not_78_out, F12);
  not not_79 (not_79_out, OP6);
  not not_80 (not_80_out, OP4);
  not not_81 (not_81_out, OP3);
  not not_82 (not_82_out, OP2);
  not not_83 (not_83_out, OP4);
  not not_84 (not_84_out, OP3);
  not not_85 (not_85_out, F13);
  not not_86 (not_86_out, F12);
  not not_87 (not_87_out, OP6);
  not not_88 (not_88_out, OP5);
  not not_89 (not_89_out, OP4);
  not not_90 (not_90_out, OP3);
  not not_91 (not_91_out, OP2);
  not not_92 (not_92_out, OP6);
  not not_93 (not_93_out, OP3);
  not not_94 (not_94_out, F30);
  not not_95 (not_95_out, F25);
  not not_96 (not_96_out, F14);
  not not_97 (not_97_out, F13);
  not not_98 (not_98_out, F12);
  not not_99 (not_99_out, OP6);
  not not_100 (not_100_out, OP3);
  not not_101 (not_101_out, OP2);
  not not_102 (not_102_out, F25);
  not not_103 (not_103_out, F14);
  not not_104 (not_104_out, F13);
  not not_105 (not_105_out, F12);
  not not_106 (not_106_out, OP6);
  not not_107 (not_107_out, OP3);
  not not_108 (not_108_out, OP2);
  not not_109 (not_109_out, F30);
  not not_110 (not_110_out, F25);
  not not_111 (not_111_out, OP6);
  not not_112 (not_112_out, OP3);
  not not_113 (not_113_out, OP2);
  not not_114 (not_114_out, F30);
  not not_115 (not_115_out, F25);
  not not_116 (not_116_out, F12);
  not not_117 (not_117_out, OP6);
  not not_118 (not_118_out, OP3);
  not not_119 (not_119_out, OP2);
  not not_120 (not_120_out, F30);
  not not_121 (not_121_out, F25);
  not not_122 (not_122_out, F14);
  not not_123 (not_123_out, F12);
  not not_124 (not_124_out, OP6);
  not not_125 (not_125_out, OP3);
  not not_126 (not_126_out, OP2);
  not not_127 (not_127_out, F30);
  not not_128 (not_128_out, F25);
  not not_129 (not_129_out, F14);
  not not_130 (not_130_out, OP6);
  not not_131 (not_131_out, OP3);
  not not_132 (not_132_out, OP2);
  not not_133 (not_133_out, F14);
  not not_134 (not_134_out, F13);
  not not_135 (not_135_out, F12);
  not not_136 (not_136_out, OP6);
  not not_137 (not_137_out, OP5);
  not not_138 (not_138_out, OP3);
  not not_139 (not_139_out, OP2);
  not not_140 (not_140_out, OP6);
  not not_141 (not_141_out, OP5);
  not not_142 (not_142_out, OP3);
  not not_143 (not_143_out, OP2);
  not not_144 (not_144_out, F12);
  not not_145 (not_145_out, OP6);
  not not_146 (not_146_out, OP5);
  not not_147 (not_147_out, OP3);
  not not_148 (not_148_out, OP2);
  not not_149 (not_149_out, F13);
  not not_150 (not_150_out, F12);
  not not_151 (not_151_out, OP6);
  not not_152 (not_152_out, OP5);
  not not_153 (not_153_out, OP3);
  not not_154 (not_154_out, OP2);
  not not_155 (not_155_out, F14);
  not not_156 (not_156_out, F12);
  not not_157 (not_157_out, OP6);
  not not_158 (not_158_out, OP5);
  not not_159 (not_159_out, OP3);
  not not_160 (not_160_out, OP2);
  not not_161 (not_161_out, F30);
  not not_162 (not_162_out, F25);
  not not_163 (not_163_out, F14);
  not not_164 (not_164_out, F13);
  not not_165 (not_165_out, OP6);
  not not_166 (not_166_out, OP5);
  not not_167 (not_167_out, OP3);
  not not_168 (not_168_out, OP2);
  not not_169 (not_169_out, F30);
  not not_170 (not_170_out, F25);
  not not_171 (not_171_out, F13);
  not not_172 (not_172_out, OP6);
  not not_173 (not_173_out, OP5);
  not not_174 (not_174_out, OP3);
  not not_175 (not_175_out, OP2);
  not not_176 (not_176_out, F25);
  not not_177 (not_177_out, F13);
  not not_178 (not_178_out, OP6);
  not not_179 (not_179_out, OP5);
  not not_180 (not_180_out, OP3);
  not not_181 (not_181_out, OP2);
  not not_182 (not_182_out, F14);
  not not_183 (not_183_out, F12);
  not not_184 (not_184_out, OP6);
  not not_185 (not_185_out, OP5);
  not not_186 (not_186_out, OP4);
  not not_187 (not_187_out, OP3);
  not not_188 (not_188_out, OP2);
  not not_189 (not_189_out, OP4);
  not not_190 (not_190_out, OP4);
  not not_191 (not_191_out, OP3);
  not not_192 (not_192_out, F12);
  not not_193 (not_193_out, OP3);
  not not_194 (not_194_out, OP2);
  not not_195 (not_195_out, OP3);
  not not_196 (not_196_out, OP2);
  not not_197 (not_197_out, F30);
  not not_198 (not_198_out, F25);
  not not_199 (not_199_out, F13);
  not not_200 (not_200_out, F12);
  not not_201 (not_201_out, OP6);
  not not_202 (not_202_out, OP3);
  not not_203 (not_203_out, OP2);
  not not_204 (not_204_out, OP6);
  not not_205 (not_205_out, OP3);
  not not_206 (not_206_out, F13);
  not not_207 (not_207_out, F12);
  not not_208 (not_208_out, OP6);
  not not_209 (not_209_out, OP5);
  not not_210 (not_210_out, OP4);
  not not_211 (not_211_out, OP3);
  not not_212 (not_212_out, OP2);
  not not_213 (not_213_out, F30);
  not not_214 (not_214_out, F25);
  not not_215 (not_215_out, F14);
  not not_216 (not_216_out, F13);
  not not_217 (not_217_out, F12);
  not not_218 (not_218_out, OP3);
  not not_219 (not_219_out, OP2);
  not not_220 (not_220_out, F14);
  not not_221 (not_221_out, F12);
  not not_222 (not_222_out, OP6);
  not not_223 (not_223_out, OP4);
  not not_224 (not_224_out, OP3);
  not not_225 (not_225_out, OP2);
  not not_226 (not_226_out, F14);
  not not_227 (not_227_out, F13);
  not not_228 (not_228_out, F12);
  not not_229 (not_229_out, OP4);
  not not_230 (not_230_out, OP3);
  not not_231 (not_231_out, OP2);
  not not_232 (not_232_out, F14);
  not not_233 (not_233_out, F13);
  not not_234 (not_234_out, OP4);
  not not_235 (not_235_out, OP3);
  not not_236 (not_236_out, OP2);
  not not_237 (not_237_out, OP4);
  not not_238 (not_238_out, OP3);
  not not_239 (not_239_out, OP4);
  not not_240 (not_240_out, F13);
  not not_241 (not_241_out, OP4);
  not not_242 (not_242_out, OP3);
  not not_243 (not_243_out, OP2);
  and and_1 (and_1_out, not_1_out, F13, not_2_out, not_3_out, not_4_out, not_5_out, not_6_out, not_7_out);
  and and_2 (and_2_out, F14, not_8_out, not_9_out, not_10_out, not_11_out, not_12_out, not_13_out, not_14_out);
  and and_3 (MemWrite, not_15_out, F13, not_16_out, not_17_out, OP5, not_18_out, not_19_out, not_20_out);
  and and_4 (and_4_out, not_21_out, not_22_out, not_23_out, not_24_out, not_25_out, OP4, not_26_out, not_27_out);
  and and_5 (and_5_out, F14, F13, F12, not_28_out, not_29_out, OP4, not_30_out, not_31_out);
  and and_6 (and_6_out, F14, F13, not_32_out, not_33_out, not_34_out, OP4, not_35_out, not_36_out);
  and and_7 (and_7_out, F14, not_37_out, not_38_out, not_39_out, not_40_out, OP4, not_41_out, not_42_out);
  and and_8 (and_8_out, not_43_out, F13, not_44_out, not_45_out, not_46_out, OP4, not_47_out, not_48_out);
  and and_9 (and_9_out, not_49_out, not_50_out, not_51_out, not_52_out, F12, not_53_out, not_54_out, OP4, not_55_out, not_56_out);
  and and_10 (and_10_out, not_57_out, not_58_out, F14, not_59_out, F12, not_60_out, not_61_out, OP4, not_62_out, not_63_out);
  and and_11 (and_11_out, F30, not_64_out, F14, not_65_out, F12, not_66_out, not_67_out, OP4, not_68_out, not_69_out);
  and and_12 (and_12_out, not_70_out, F13, not_71_out, not_72_out, not_73_out, not_74_out, not_75_out, not_76_out);
  and and_13 (and_13_out, not_77_out, F13, not_78_out, not_79_out, OP5, not_80_out, not_81_out, not_82_out);
  and and_14 (and_14_out, OP6, OP5, not_83_out, not_84_out, OP2);
  and and_15 (Byte, F14, not_85_out, not_86_out, not_87_out, not_88_out, not_89_out, not_90_out, not_91_out);
  and and_16 (U_Type, not_92_out, OP5, OP4, not_93_out, OP2);
  and and_17 (and_17_out, not_94_out, not_95_out, not_96_out, not_97_out, not_98_out, not_99_out, OP5, OP4, not_100_out, not_101_out);
  and and_18 (and_18_out, F30, not_102_out, not_103_out, not_104_out, not_105_out, not_106_out, OP5, OP4, not_107_out, not_108_out);
  and and_19 (and_19_out, not_109_out, not_110_out, F14, F13, F12, not_111_out, OP5, OP4, not_112_out, not_113_out);
  and and_20 (and_20_out, not_114_out, not_115_out, F14, F13, not_116_out, not_117_out, OP5, OP4, not_118_out, not_119_out);
  and and_21 (and_21_out, not_120_out, not_121_out, not_122_out, F13, not_123_out, not_124_out, OP5, OP4, not_125_out, not_126_out);
  and and_22 (and_22_out, not_127_out, not_128_out, not_129_out, F13, F12, not_130_out, OP5, OP4, not_131_out, not_132_out);
  and and_23 (and_23_out, not_133_out, not_134_out, not_135_out, not_136_out, not_137_out, OP4, not_138_out, not_139_out);
  and and_24 (and_24_out, F14, F13, F12, not_140_out, not_141_out, OP4, not_142_out, not_143_out);
  and and_25 (and_25_out, F14, F13, not_144_out, not_145_out, not_146_out, OP4, not_147_out, not_148_out);
  and and_26 (and_26_out, F14, not_149_out, not_150_out, not_151_out, not_152_out, OP4, not_153_out, not_154_out);
  and and_27 (and_27_out, not_155_out, F13, not_156_out, not_157_out, not_158_out, OP4, not_159_out, not_160_out);
  and and_28 (and_28_out, not_161_out, not_162_out, not_163_out, not_164_out, F12, not_165_out, not_166_out, OP4, not_167_out, not_168_out);
  and and_29 (and_29_out, not_169_out, not_170_out, F14, not_171_out, F12, not_172_out, not_173_out, OP4, not_174_out, not_175_out);
  and and_30 (and_30_out, F30, not_176_out, F14, not_177_out, F12, not_178_out, not_179_out, OP4, not_180_out, not_181_out);
  and and_31 (and_31_out, not_182_out, F13, not_183_out, not_184_out, not_185_out, not_186_out, not_187_out, not_188_out);
  and and_32 (and_32_out, OP6, OP5, not_189_out, OP3, OP2);
  and and_33 (and_33_out, OP6, OP5, not_190_out, not_191_out, OP2);
  and and_34 (and_34_out, F14, F13, not_192_out, OP6, OP5, OP4, not_193_out, not_194_out);
  and and_35 (and_35_out, F14, F13, F12, OP6, OP5, OP4, not_195_out, not_196_out);
  and and_36 (and_36_out, not_197_out, not_198_out, F14, not_199_out, not_200_out, not_201_out, OP5, OP4, not_202_out, not_203_out);
  and and_37 (and_37_out, not_204_out, OP5, OP4, not_205_out, OP2);
  and and_38 (and_38_out, F14, not_206_out, not_207_out, not_208_out, not_209_out, not_210_out, not_211_out, not_212_out);
  and and_39 (ecall, not_213_out, not_214_out, not_215_out, not_216_out, not_217_out, OP6, OP5, OP4, not_218_out, not_219_out);
  and and_40 (S_Type, not_220_out, F13, not_221_out, not_222_out, OP5, not_223_out, not_224_out, not_225_out);
  and and_41 (BEQ, not_226_out, not_227_out, not_228_out, OP6, OP5, not_229_out, not_230_out, not_231_out);
  and and_42 (BNE, not_232_out, not_233_out, F12, OP6, OP5, not_234_out, not_235_out, not_236_out);
  and and_43 (JALR, OP6, OP5, not_237_out, not_238_out, OP2);
  and and_44 (JAL, OP6, OP5, not_239_out, OP3, OP2);
  and and_45 (BGE, F14, not_240_out, F12, OP6, OP5, not_241_out, not_242_out, not_243_out);
  or or_1 (MemToReg, and_1_out, and_2_out);
  or or_2 (ALU_SRC, and_4_out, and_5_out, and_6_out, and_7_out, and_8_out, and_9_out, and_10_out, and_11_out, and_12_out, and_13_out, and_14_out);
  or or_3 (RegWrite, and_17_out, and_18_out, and_19_out, and_20_out, and_21_out, and_22_out, and_23_out, and_24_out, and_25_out, and_26_out, and_27_out, and_28_out, and_29_out, and_30_out, and_31_out, and_32_out, and_33_out, and_34_out, and_35_out, and_36_out, and_37_out, and_38_out);
endmodule

// ALU
module ALU (
  input  [31:0] X,
  input  [31:0] Y,
  input  [3:0] AluOP,
  output out_4,
  output Equal,
  output out_6,
  output [31:0] Result,
  output [31:0] Result_2
);

  wire [0:0] comparator_1_lt, comparator_2_lt;
  wire [31:0] adder_1_out, AND_out, divider_1_out, divider_1_rem, multiplier_1_cout, multiplier_1_out,
       NOR_out, OR_out, shifter_1_out, shifter_2_out, shifter_3_out, subtractor_1_out, XOR_out;

  assign AND_out = X & Y;  // AND_Gate AND, 32 bits wide
  assign OR_out = X | Y;  // OR_Gate OR, 32 bits wide
  Shifter #(.width(32)) shifter_1 (.in(X), .\dist (Y[4:0]), .out(shifter_1_out));
  Shifter #(.width(32), .shift("ar")) shifter_2 (.in(X), .\dist (Y[4:0]), .out(shifter_2_out));
  Shifter #(.width(32), .shift("lr")) shifter_3 (.in(X), .\dist (Y[4:0]), .out(shifter_3_out));
  Multiplier #(.width(32)) multiplier_1 (.a(X), .b(Y), .out(multiplier_1_out), .cout(multiplier_1_cout));  // open: cin
  Divider #(.width(32)) divider_1 (.a(X), .b(Y), .out(divider_1_out), .rem(divider_1_rem));  // open: upper
  Adder #(.width(32)) adder_1 (.a(X), .b(Y), .out(adder_1_out));  // open: cin, cout
  Subtractor #(.width(32)) subtractor_1 (.a(X), .b(Y), .out(subtractor_1_out));  // open: bin, bout
  assign XOR_out = X ^ Y;  // XOR_Gate XOR, 32 bits wide
  assign NOR_out = ~(X | Y);  // NOR_Gate NOR, 32 bits wide
  Comparator #(.width(32)) comparator_1 (.a(X), .b(Y), .eq(Equal), .lt(comparator_1_lt[0]));  // open: gt
  Comparator #(.width(32), .mode("unsigned")) comparator_2 (.a(X), .b(Y), .lt(comparator_2_lt[0]));  // open: gt, eq
  Multiplexer #(.select(4), .width(32), .enable("false")) multiplexer_1 (
    .in0(shifter_1_out), .in1(shifter_2_out), .in2(shifter_3_out), .in3(multiplier_1_out),
    .in4(divider_1_out), .in5(adder_1_out), .in6(subtractor_1_out), .in7(AND_out), .in8(OR_out),
    .in9(XOR_out), .in10(NOR_out), .in11({{31{1'b0}}, comparator_1_lt[0]}),
    .in12({{31{1'b0}}, comparator_2_lt[0]}), .in13({32{1'b0}}), .in14({32{1'b0}}), .in15({32{1'b0}}),
    .out(Result), .sel(AluOP));
  Multiplexer #(.select(4), .width(32), .enable("false")) multiplexer_2 (
    .in0({32{1'b0}}), .in1({32{1'b0}}), .in2({32{1'b0}}), .in3(multiplier_1_cout), .in4(divider_1_rem),
    .in5({32{1'b0}}), .in6({32{1'b0}}), .in7({32{1'b0}}), .in8({32{1'b0}}), .in9({32{1'b0}}),
    .in10({32{1'b0}}), .in11({32{1'b0}}), .in12({32{1'b0}}), .in13({32{1'b0}}), .in14({32{1'b0}}),
    .in15({32{1'b0}}), .out(Result_2), .sel(AluOP));
  Multiplexer #(.select(4), .enable("false")) multiplexer_3 (
    .in0(1'b0), .in1(1'b0), .in2(1'b0), .in3(1'b0), .in4(1'b0), .in5(1'b0), .in6(1'b0), .in7(1'b0),
    .in8(1'b0), .in9(1'b0), .in10(1'b0), .in11(comparator_1_lt[0]), .in12(comparator_2_lt[0]), .in13(1'b0),
    .in14(1'b0), .in15(1'b0), .out(out_6), .sel(AluOP));
  not not_1 (out_4, out_6);

  // Other names for the same wires on the sheet: Result2[31:0] = Result_2; S[3:0] = AluOP; tunnel = out_6;
  //   tunnel_t = out_4

  // Notes on the sheet:
  //   不要改变此引脚区域内容，也不要改变ALU封装形式
  //   输入引脚
  //   输出引脚
endmodule

module Regifile (
  input  [31:0] Din,
  input  Clk,
  input  WE,
  input  [4:0] R1_num,
  input  [4:0] W_num,
  input  [4:0] R2_num,
  output [31:0] R1,
  output [31:0] R2
);

  // RegisterFile registerfile_1: pin names not known; wires that end beside it: Din, Clk, WE, W_num, R1_num, R2_num, R1, R2
endmodule

module \理想流水线  (
  output RegWrite,
  output MemWrite,
  output [31:0] IF_PC,
  output [31:0] ID_PC,
  output [31:0] EX_PC,
  output [31:0] M_PC,
  output [31:0] WB_PC,
  output [31:0] RDin,
  output [31:0] MDin,
  output [31:0] LedData
);

  wire AddrFromImm, and_1_out, and_3_out, and_4_out, and_5_out, BEQ_EX, BGE_EX, BNE_EX, Byte_MEM, CLK,
       clock_1_out, comparator_1_eq, comparator_2_eq, comparator_2_lt, d_ff_1_q, ecall, equal,
       ex_mem_1_memwriteout, ex_mem_1_regwriteout, gequal, Go, halt, id_ex_1_alusrcbout, id_ex_1_byteout,
       id_ex_1_memtoregout, id_ex_1_memwriteout, id_ex_1_regwriteout, id_ex_1_utypeout, IR1, IR2, IR3,
       JAL_EX, JAL_MEM, JALR_EX, JALR_MEM, mem_wb_1_regwriteout, MemToReg_MEM, nand_1_out, not_1_out,
       not_2_out, not_3_out, not_4_out, RST, SaveBreakPoint, URET_EX, UType_MEM, W1, W2, W3,
       \单周期硬布线控制器_1_alu_src , \单周期硬布线控制器_1_beq , \单周期硬布线控制器_1_bge , \单周期硬布线控制器_1_bne , \单周期硬布线控制器_1_byte ,
       \单周期硬布线控制器_1_jal , \单周期硬布线控制器_1_jalr , \单周期硬布线控制器_1_memtoreg , \单周期硬布线控制器_1_memwrite ,
       \单周期硬布线控制器_1_regwrite , \单周期硬布线控制器_1_u_type , \单周期硬布线控制器_1_uret , \立即数类型识别器_1_b , \立即数类型识别器_1_i ,
       \立即数类型识别器_1_j , \立即数类型识别器_1_s , \立即数类型识别器_1_u ;
  wire [0:0] alu_1_result;
  wire [2:0] priority_encoder_1_out, priority_encoder_2_out, priority_encoder_3_out;
  wire [3:0] id_ex_1_aluopout, \单周期硬布线控制器_1_alu_op ;
  wire [4:0] ex_mem_1_rtagout, id_ex_1_rtagout, mem_wb_1_rtagout, multiplexer_1_out, multiplexer_2_out;
  wire [7:0] multiplexer_6_out;
  wire [11:0] if_id_1_irout;
  wire [12:0] CNT_num;
  wire [15:0] \LoadUse次数 , \总周期数 , \插入气泡数 , \无条件分支数 , \条件分支成功数 ;
  wire [31:0] a0, a7, adder_1_out, adder_2_out, adder_3_out, adder_4_out, bit_extender_1_out,
       bit_extender_2_out, bit_extender_3_out, bit_extender_4_out, EX_IR, ex_mem_1_immout, ex_mem_1_pcout,
       ex_mem_1_resultout, id_ex_1_immout, id_ex_1_pcout, id_ex_1_r1out, id_ex_1_r2out, ID_IR, if_id_1_pcout,
       IF_IR, MEM_IR, mem_wb_1_writedataout, multiplexer_3_out, multiplexer_4_out, multiplexer_5_out,
       multiplexer_7_out, PC_q, ram_1_data, rom_1_data, WB_IR;
  wire [31:1] alu_1_result_2;
  wire [31:12] if_id_1_irout_2;

  Button \u_总复位  (.out(RST));
  Button _1 (.out(IR1));
  Button _2 (.out(IR2));
  Button _3 (.out(IR3));
  // Probe on \总周期数 
  // Probe on \总周期数 
  Button \u_继续运行  (.out(Go));
  LED led_1 (.in(W1));
  LED led_2 (.in(W2));
  LED led_3 (.in(W3));
  Hex_Digit_Display hex_digit_display_1 (.value(LedData[31:28]));  // open: dp
  // Probe on IF_PC[19:0]
  // RiscV_Probe riscv_probe_1: pin names not known; wires that end beside it: IF_IR
  not not_1 (not_1_out, halt);
  Hex_Digit_Display hex_digit_display_2 (.value(LedData[27:24]));  // open: dp
  Hex_Digit_Display hex_digit_display_3 (.value(LedData[23:20]));  // open: dp
  // Probe on ID_PC[19:0]
  // RiscV_Probe riscv_probe_2: pin names not known; wires that end beside it: ID_IR
  Register #(.width(32), .Select("low")) PC (.D(multiplexer_4_out), .en(not_1_out), .Q(PC_q), .clr(RST));  // open: clk
  Hex_Digit_Display hex_digit_display_4 (.value(LedData[15:12]));  // open: dp
  Hex_Digit_Display hex_digit_display_5 (.value(LedData[19:16]));  // open: dp
  Hex_Digit_Display hex_digit_display_6 (.value(LedData[11:8]));  // open: dp
  Hex_Digit_Display hex_digit_display_7 (.value(LedData[7:4]));  // open: dp
  // Probe on EX_PC[19:0]
  // RiscV_Probe riscv_probe_3: pin names not known; wires that end beside it: EX_IR
  // RiscV_Probe riscv_probe_4: pin names not known
  ROM #(.addrWidth(10), .dataWidth(32), .Select("high")) rom_1 (.addr(PC_q[11:2]), .data(rom_1_data));
  Hex_Digit_Display hex_digit_display_8 (.value(LedData[3:0]));  // open: dp
  IF_ID if_id_1 (
    .IRin(rom_1_data), .PCin(PC_q), .IRout({if_id_1_irout_2, if_id_1_irout}), .PCout(if_id_1_pcout));  // open: CLK, RST
  // Probe on \总周期数 
  // Probe on M_PC[19:0]
  // RiscV_Probe riscv_probe_5: pin names not known; wires that end beside it: MEM_IR
  // Probe on \总周期数 
  // Probe on \无条件分支数 
  // Probe on \条件分支成功数 
  // Probe on \插入气泡数 
  // Probe on \LoadUse次数 
  Comparator #(.width(32)) comparator_1 (.a(a7), .b(32'h22), .eq(comparator_1_eq));  // open: gt, lt
  // Probe on IF_PC[11:0]
  // Probe on WB_PC[19:0]
  // RiscV_Probe riscv_probe_6: pin names not known; wires that end beside it: WB_IR
  \单周期硬布线控制器  \u_单周期硬布线控制器_1  (
    .Funct({if_id_1_irout_2[30], if_id_1_irout_2[25], if_id_1_irout_2[14:12]}), .OP(if_id_1_irout[6:2]),
    .ALU_OP(\单周期硬布线控制器_1_alu_op ), .MemToReg(\单周期硬布线控制器_1_memtoreg ), .MemWrite(\单周期硬布线控制器_1_memwrite ),
    .ALU_SRC(\单周期硬布线控制器_1_alu_src ), .RegWrite(\单周期硬布线控制器_1_regwrite ), .ecall(ecall),
    .Jalr(\单周期硬布线控制器_1_jalr ), .Beq(\单周期硬布线控制器_1_beq ), .JAL(\单周期硬布线控制器_1_jal ), .Bne(\单周期硬布线控制器_1_bne ),
    .in_3(if_id_1_irout_2[21]), .uret(\单周期硬布线控制器_1_uret ), .BGE(\单周期硬布线控制器_1_bge ),
    .Byte(\单周期硬布线控制器_1_byte ), .U_Type(\单周期硬布线控制器_1_u_type ));  // open: S_type
  Multiplexer #(.width(5), .enable("false")) multiplexer_1 (
    .in0(if_id_1_irout_2[19:15]), .in1(5'b01010), .out(multiplexer_1_out), .sel(ecall));
  Multiplexer #(.width(5), .enable("false")) multiplexer_2 (
    .in0(if_id_1_irout_2[24:20]), .in1(5'b10001), .out(multiplexer_2_out), .sel(ecall));
  \立即数类型识别器  \u_立即数类型识别器_1  (
    .I(\立即数类型识别器_1_i ), .S(\立即数类型识别器_1_s ), .B(\立即数类型识别器_1_b ), .J(\立即数类型识别器_1_j ), .U(\立即数类型识别器_1_u ));  // open: OP, Funct
  and and_1 (and_1_out, ecall, comparator_1_eq);
  // Probe on EX_PC[11:0]
  // Probe on ID_PC[11:0]
  Priority_Encoder priority_encoder_1 (
    .in0(\立即数类型识别器_1_i ), .in1(\立即数类型识别器_1_s ), .in2(\立即数类型识别器_1_b ), .in3(\立即数类型识别器_1_j ),
    .in4(\立即数类型识别器_1_u ), .in5(1'b0), .in6(1'b0), .in7(1'b0), .out(priority_encoder_1_out));  // open: gs, en_out, en_in
  assign bit_extender_1_out = {{20{if_id_1_irout_2[31]}}, if_id_1_irout_2[31:20]};  // Bit_Extender bit_extender_1
  assign bit_extender_2_out = {{20{if_id_1_irout_2[31]}}, {if_id_1_irout_2[31:25], if_id_1_irout[11:7]}};  // Bit_Extender bit_extender_2
  assign bit_extender_3_out = {{20{if_id_1_irout[7]}}, {if_id_1_irout[7], if_id_1_irout_2[30:25], if_id_1_irout[11:8], 1'b0}};  // Bit_Extender bit_extender_3
  assign bit_extender_4_out = {{12{if_id_1_irout_2[19]}}, {if_id_1_irout_2[19:12], if_id_1_irout_2[20], if_id_1_irout_2[30:21], 1'b0}};  // Bit_Extender bit_extender_4
  Register #(.width(32), .Select("low")) register_1 (.D(a0), .en(and_1_out), .Q(LedData), .clk(CLK), .clr(RST));
  // Probe on M_PC[11:0]
  D_Flip_Flop #(.trigger("high"), .Pre_Clr_Positions("LEGACY"), .enable("true"), .NewFFLayout("false")) d_ff_1 (.Q(d_ff_1_q));  // open: clk, D, Qn, preset, en, reset
  // Probe on 13'hc
  // Probe on WB_PC[11:0]
  Comparator #(.width(13)) comparator_2 (
    .a(CNT_num), .b(13'hc), .eq(comparator_2_eq), .lt(comparator_2_lt));  // open: gt
  Clock clock_1 (.out(clock_1_out));
  Regifile regifile_1 (
    .Din(mem_wb_1_writedataout), .R1(a0), .R2(a7), .WE(mem_wb_1_regwriteout), .W_num(mem_wb_1_rtagout),
    .R1_num(multiplexer_1_out), .R2_num(multiplexer_2_out));  // open: Clk
  Adder #(.width(32)) adder_1 (.a(PC_q), .b(bit_extender_3_out), .out(adder_1_out));  // open: cin, cout
  Adder #(.width(32)) adder_2 (.a(PC_q), .b(bit_extender_4_out), .out(adder_2_out));  // open: cin, cout
  nand nand_1 (nand_1_out, d_ff_1_q, comparator_2_eq);
  Counter #(.width(13), .max('h1fff), .ongoal("stay"), .behavior("old")) counter_1 (
    .count(comparator_2_lt), .Q(CNT_num), .clk(clock_1_out));  // open: load, D, carry, clr, preset
  not not_2 (not_2_out, comparator_1_eq);
  not not_3 (not_3_out, Go);
  assign CLK = nand_1_out ? clock_1_out : 1'bz;  // Controlled_Buffer controlled_buffer_1
  Multiplexer #(.select(3), .width(32), .enable("false")) multiplexer_3 (
    .in0(bit_extender_1_out), .in1(bit_extender_2_out), .in2(adder_1_out), .in3(adder_2_out),
    .in4({if_id_1_irout_2, {12{1'b0}}}), .out(multiplexer_3_out), .sel(priority_encoder_1_out));  // open: in5, in6, in7
  and and_2 (halt, not_2_out, ecall, not_3_out);
  Pull_Resistor #(.pull(1)) pull_resistor_1 (.node(CLK));
  ID_EX id_ex_1 (
    .Bytein(\单周期硬布线控制器_1_byte ), .BGEin(\单周期硬布线控制器_1_bge ), .URETin(\单周期硬布线控制器_1_uret ),
    .JALRin(\单周期硬布线控制器_1_jalr ), .JALin(\单周期硬布线控制器_1_jal ), .BEQin(\单周期硬布线控制器_1_beq ),
    .MemToRegin(\单周期硬布线控制器_1_memtoreg ), .MemWritein(\单周期硬布线控制器_1_memwrite ), .AluOPin(\单周期硬布线控制器_1_alu_op ),
    .AluSrcBin(\单周期硬布线控制器_1_alu_src ), .RegWritein(\单周期硬布线控制器_1_regwrite ), .UTypein(\单周期硬布线控制器_1_u_type ),
    .R1in(a0), .R2in(a7), .RTagin(if_id_1_irout[11:7]), .Immin(multiplexer_3_out), .Byteout(id_ex_1_byteout),
    .BGEout(BGE_EX), .URETout(URET_EX), .JALRout(JALR_EX), .JALout(JAL_EX), .BEQout(BEQ_EX),
    .MemToRegout(id_ex_1_memtoregout), .MemWriteout(id_ex_1_memwriteout), .AluOPout(id_ex_1_aluopout),
    .AluSrcBout(id_ex_1_alusrcbout), .RegWriteout(id_ex_1_regwriteout), .UTypeout(id_ex_1_utypeout),
    .R1out(id_ex_1_r1out), .R2out(id_ex_1_r2out), .RTagout(id_ex_1_rtagout), .Immout(id_ex_1_immout),
    .PCout(id_ex_1_pcout), .PCin(if_id_1_pcout), .BNEin(\单周期硬布线控制器_1_bne ), .BNEout(BNE_EX));  // open: CLK, RST
  Priority_Encoder priority_encoder_2 (
    .in0(1'b1), .in1(AddrFromImm), .in2(JALR_EX), .in3(URET_EX), .in4(1'b0), .in5(1'b0), .in6(1'b0),
    .in7(1'b0), .out(priority_encoder_2_out));  // open: gs, en_out, en_in
  Multiplexer #(.select(3), .width(32), .enable("false")) multiplexer_4 (
    .in0(adder_3_out), .in1(id_ex_1_immout), .in2({alu_1_result_2, 1'b0}), .out(multiplexer_4_out),
    .sel(priority_encoder_2_out));  // open: in3, in4, in5, in6, in7
  Multiplexer #(.width(32), .enable("false")) multiplexer_5 (
    .in0(id_ex_1_r2out), .in1(id_ex_1_immout), .out(multiplexer_5_out), .sel(id_ex_1_alusrcbout));
  Adder #(.width(32)) adder_3 (.a(PC_q), .b(32'h4), .out(adder_3_out));  // open: cin, cout
  not not_4 (not_4_out, equal);
  ALU alu_1 (
    .X(id_ex_1_r1out), .Y(multiplexer_5_out), .AluOP(id_ex_1_aluopout), .Equal(equal),
    .Result({alu_1_result_2, alu_1_result[0]}), .out_4(gequal));  // open: Result_2, out_6
  and and_3 (and_3_out, BNE_EX, not_4_out);
  and and_4 (and_4_out, BEQ_EX, equal);
  and and_5 (and_5_out, BGE_EX, gequal);
  or or_1 (AddrFromImm, and_3_out, and_4_out, and_5_out, JAL_EX);
  EX_MEM ex_mem_1 (
    .Bytein(id_ex_1_byteout), .MemToRegin(id_ex_1_memtoregout), .MemWritein(id_ex_1_memwriteout),
    .RegWritein(id_ex_1_regwriteout), .UTypein(id_ex_1_utypeout),
    .Resultin({alu_1_result_2, alu_1_result[0]}), .RTagin(id_ex_1_rtagout), .Byteout(Byte_MEM),
    .MemToRegout(MemToReg_MEM), .MemWriteout(ex_mem_1_memwriteout), .RegWriteout(ex_mem_1_regwriteout),
    .UTypeout(UType_MEM), .Resultout(ex_mem_1_resultout), .RTagout(ex_mem_1_rtagout), .PCin(id_ex_1_pcout),
    .PCout(ex_mem_1_pcout), .JALRin(JALR_EX), .JALRout(JALR_MEM), .JALin(JAL_EX), .JALout(JAL_MEM),
    .Immin(id_ex_1_immout), .Immout(ex_mem_1_immout));  // open: CLK, RST
  RAM #(.addrWidth(10), .dataWidth(32), .bus("separate"), .Select("high"), .simpleMode("false")) ram_1 (
    .addr(ex_mem_1_resultout[11:2]), .data(ram_1_data));  // open: din, str, sel, clk, ld, clr
  Adder #(.width(32)) adder_4 (.a(32'h4), .b(ex_mem_1_pcout), .out(adder_4_out));  // open: cin, cout
  or or_2 (SaveBreakPoint, JALR_MEM, JAL_MEM);
  Multiplexer #(.select(2), .width(8), .enable("false")) multiplexer_6 (
    .in0(ram_1_data[7:0]), .in1(ram_1_data[15:8]), .in2(ram_1_data[23:16]), .in3(ram_1_data[31:24]),
    .out(multiplexer_6_out), .sel(ex_mem_1_resultout[1:0]));
  Multiplexer #(.select(3), .width(32), .enable("false")) multiplexer_7 (
    .in0(ex_mem_1_resultout), .in1(ram_1_data), .in2(adder_4_out), .in3(ex_mem_1_immout),
    .in4({{24{1'b0}}, multiplexer_6_out}), .out(multiplexer_7_out), .sel(priority_encoder_3_out));  // open: in5, in6, in7
  Priority_Encoder priority_encoder_3 (
    .in0(1'b1), .in1(MemToReg_MEM), .in2(SaveBreakPoint), .in3(UType_MEM), .in4(Byte_MEM), .in5(1'b0),
    .in6(1'b0), .in7(1'b0), .out(priority_encoder_3_out));  // open: gs, en_out, en_in
  MEM_WB mem_wb_1 (
    .RegWritein(ex_mem_1_regwriteout), .WriteDatain(multiplexer_7_out), .RTagin(ex_mem_1_rtagout),
    .RegWriteout(mem_wb_1_regwriteout), .WriteDataout(mem_wb_1_writedataout), .RTagout(mem_wb_1_rtagout),
    .PCin(ex_mem_1_pcout));  // open: CLK, RST, PCout

  // Other names for the same wires on the sheet: MEM_PC[31:0] = M_PC

  // Notes on the sheet:
  //   中断源
  //   时空图监测，可删除
  //   中断等待指示
  //   数码管输出
  //   指令存储器
  //   指令探针
  //   contents of rom_1 (hex, n*v repeats v):
  //   313 1000e13 8400493 849493 8348493 400913 891913 490913 849493 8248493 849493 8148493 891913 490913
  //   891913 490913 932023 12484b3 430313 fffe0e13 fe0e18e3 2000e13 313 34483 900533 2200893 73 130313
  //   fffe0e13 fe0e14e3 a00893 73
  //   指令字
  //   BType-Imm
  //   JType-Imm
  //   UType-Imm
  //   LED显示&halt控制
  //   IType-Imm
  //   SType-Imm
  //   控制位
  //   流水调试日志用
  //   暂停节拍，不能为0
  //   戳工具置1进入计数暂停模式，ctrl+k时钟自动运行到对应节拍暂停
  //   ctrl+k关闭时钟连续运行，将控制位置零，进入单步调试模式调试
  //   用这个时钟源需要去掉电路中的其他时钟源
  //   可计数暂停的时钟源
  //   Byte
  //   BGE
  //   URET
  //   JALR
  //   JAL
  //   Beq
  //   Bne
  //   MemToReg
  //   MemWrite
  //   AluOP
  //   AluSrcB
  //   RegWrite
  //   UType
  //   为方便自动评测，需要输出流水线各段保存的PC值，注意是PC不是PC+4，另外ID段寄存器写入信息，Mem段内存写入信息也要输出
  //   数据存储器
endmodule

module \气泡流水线  (
  output RegWrite,
  output MemWrite,
  output [31:0] IF_PC,
  output [31:0] ID_PC,
  output [31:0] EX_PC,
  output [31:0] M_PC,
  output [31:0] WB_PC,
  output [31:0] RDin,
  output [31:0] MDin,
  output [31:0] LedData
);

  wire CLK, clock_1_out, comparator_1_eq, comparator_1_lt, d_ff_1_q, Go, IR1, IR2, IR3, nand_1_out, RST, W1,
       W2, W3;
  wire [12:0] CNT_num;
  wire [15:0] \LoadUse次数 , \总周期数 , \插入气泡数 , \无条件分支数 , \条件分支成功数 ;
  wire [31:0] EX_IR, ID_IR, IF_IR, MEM_IR, WB_IR;

  Button \u_总复位  (.out(RST));
  Button _1 (.out(IR1));
  Button _2 (.out(IR2));
  Button _3 (.out(IR3));
  // Probe on \总周期数 
  // Probe on \总周期数 
  Button \u_继续运行  (.out(Go));
  LED led_1 (.in(W1));
  LED led_2 (.in(W2));
  LED led_3 (.in(W3));
  Hex_Digit_Display hex_digit_display_1 (.value(LedData[31:28]));  // open: dp
  // Probe on IF_PC[19:0]
  // RiscV_Probe riscv_probe_1: pin names not known; wires that end beside it: IF_IR
  Hex_Digit_Display hex_digit_display_2 (.value(LedData[23:20]));  // open: dp
  Hex_Digit_Display hex_digit_display_3 (.value(LedData[27:24]));  // open: dp
  // Probe on ID_PC[19:0]
  // RiscV_Probe riscv_probe_2: pin names not known; wires that end beside it: ID_IR
  Hex_Digit_Display hex_digit_display_4 (.value(LedData[15:12]));  // open: dp
  Hex_Digit_Display hex_digit_display_5 (.value(LedData[19:16]));  // open: dp
  Hex_Digit_Display hex_digit_display_6 (.value(LedData[7:4]));  // open: dp
  Hex_Digit_Display hex_digit_display_7 (.value(LedData[11:8]));  // open: dp
  // Probe on EX_PC[19:0]
  // RiscV_Probe riscv_probe_3: pin names not known; wires that end beside it: EX_IR
  Hex_Digit_Display hex_digit_display_8 (.value(LedData[3:0]));  // open: dp
  // Probe on \总周期数 
  // Probe on M_PC[19:0]
  // RiscV_Probe riscv_probe_4: pin names not known; wires that end beside it: MEM_IR
  // Probe on \总周期数 
  // Probe on \无条件分支数 
  // Probe on \条件分支成功数 
  // Probe on \插入气泡数 
  // Probe on \LoadUse次数 
  // Probe on IF_PC[11:0]
  // Probe on WB_PC[19:0]
  // RiscV_Probe riscv_probe_5: pin names not known; wires that end beside it: WB_IR
  // Probe on ID_PC[11:0]
  // Probe on EX_PC[11:0]
  // Probe on M_PC[11:0]
  D_Flip_Flop #(.trigger("high"), .Pre_Clr_Positions("LEGACY"), .enable("true"), .NewFFLayout("false")) d_ff_1 (.Q(d_ff_1_q));  // open: clk, D, Qn, preset, en, reset
  // Probe on 13'hc
  // Probe on WB_PC[11:0]
  Comparator #(.width(13)) comparator_1 (
    .a(CNT_num), .b(13'hc), .eq(comparator_1_eq), .lt(comparator_1_lt));  // open: gt
  Clock clock_1 (.out(clock_1_out));
  nand nand_1 (nand_1_out, d_ff_1_q, comparator_1_eq);
  Counter #(.width(13), .max('h1fff), .ongoal("stay"), .behavior("old")) counter_1 (
    .count(comparator_1_lt), .Q(CNT_num), .clk(clock_1_out));  // open: load, D, carry, clr, preset
  assign CLK = nand_1_out ? clock_1_out : 1'bz;  // Controlled_Buffer controlled_buffer_1
  Pull_Resistor #(.pull(1)) pull_resistor_1 (.node(CLK));

  // Other names for the same wires on the sheet: MEM_PC[31:0] = M_PC

  // Notes on the sheet:
  //   中断源
  //   时空图监测，可删除
  //   中断等待指示
  //   数码管输出
  //   控制位
  //   流水调试日志用
  //   暂停节拍，不能为0
  //   戳工具置1进入计数暂停模式，ctrl+k时钟自动运行到对应节拍暂停
  //   ctrl+k关闭时钟连续运行，将控制位置零，进入单步调试模式调试
  //   可计数暂停的时钟源
  //   为方便自动评测，需要输出流水线各段保存的PC值，注意是PC不是PC+4，另外ID段寄存器写入信息，Mem段内存写入信息也要输出
endmodule

module \重定向流水线  (
  output RegWrite,
  output MemWrite,
  output [31:0] IF_PC,
  output [31:0] ID_PC,
  output [31:0] EX_PC,
  output [31:0] M_PC,
  output [31:0] WB_PC,
  output [31:0] RDin,
  output [31:0] MDin,
  output [31:0] LedData
);

  wire CLK, clock_1_out, comparator_1_eq, comparator_1_lt, d_ff_1_q, Go, IR1, IR2, IR3, nand_1_out, RST, W1,
       W2, W3;
  wire [12:0] CNT_num;
  wire [15:0] \LoadUse次数 , \总周期数 , \插入气泡数 , \无条件分支数 , \条件分支成功数 ;
  wire [31:0] EX_IR, ID_IR, IF_IR, MEM_IR, WB_IR;

  Button \u_总复位  (.out(RST));
  Button _1 (.out(IR1));
  Button _2 (.out(IR2));
  Button _3 (.out(IR3));
  // Probe on \总周期数 
  // Probe on \总周期数 
  Button \u_继续运行  (.out(Go));
  LED led_1 (.in(W1));
  LED led_2 (.in(W2));
  LED led_3 (.in(W3));
  Hex_Digit_Display hex_digit_display_1 (.value(LedData[31:28]));  // open: dp
  // Probe on IF_PC[19:0]
  // RiscV_Probe riscv_probe_1: pin names not known; wires that end beside it: IF_IR
  Hex_Digit_Display hex_digit_display_2 (.value(LedData[23:20]));  // open: dp
  Hex_Digit_Display hex_digit_display_3 (.value(LedData[27:24]));  // open: dp
  // Probe on ID_PC[19:0]
  // RiscV_Probe riscv_probe_2: pin names not known; wires that end beside it: ID_IR
  Hex_Digit_Display hex_digit_display_4 (.value(LedData[15:12]));  // open: dp
  Hex_Digit_Display hex_digit_display_5 (.value(LedData[19:16]));  // open: dp
  Hex_Digit_Display hex_digit_display_6 (.value(LedData[7:4]));  // open: dp
  Hex_Digit_Display hex_digit_display_7 (.value(LedData[11:8]));  // open: dp
  // Probe on EX_PC[19:0]
  // RiscV_Probe riscv_probe_3: pin names not known; wires that end beside it: EX_IR
  Hex_Digit_Display hex_digit_display_8 (.value(LedData[3:0]));  // open: dp
  // Probe on \总周期数 
  // Probe on M_PC[19:0]
  // RiscV_Probe riscv_probe_4: pin names not known; wires that end beside it: MEM_IR
  // Probe on \总周期数 
  // Probe on \无条件分支数 
  // Probe on \条件分支成功数 
  // Probe on \插入气泡数 
  // Probe on \LoadUse次数 
  // Probe on IF_PC[11:0]
  // Probe on WB_PC[19:0]
  // RiscV_Probe riscv_probe_5: pin names not known; wires that end beside it: WB_IR
  // Probe on EX_PC[11:0]
  // Probe on ID_PC[11:0]
  // Probe on M_PC[11:0]
  D_Flip_Flop #(.trigger("high"), .Pre_Clr_Positions("LEGACY"), .enable("true"), .NewFFLayout("false")) d_ff_1 (.Q(d_ff_1_q));  // open: clk, D, Qn, preset, en, reset
  // Probe on 13'hc
  // Probe on WB_PC[11:0]
  Comparator #(.width(13)) comparator_1 (
    .a(CNT_num), .b(13'hc), .eq(comparator_1_eq), .lt(comparator_1_lt));  // open: gt
  Clock clock_1 (.out(clock_1_out));
  nand nand_1 (nand_1_out, d_ff_1_q, comparator_1_eq);
  Counter #(.width(13), .max('h1fff), .ongoal("stay"), .behavior("old")) counter_1 (
    .count(comparator_1_lt), .Q(CNT_num), .clk(clock_1_out));  // open: load, D, carry, clr, preset
  assign CLK = nand_1_out ? clock_1_out : 1'bz;  // Controlled_Buffer controlled_buffer_1
  Pull_Resistor #(.pull(1)) pull_resistor_1 (.node(CLK));

  // Other names for the same wires on the sheet: MEM_PC[31:0] = M_PC

  // Notes on the sheet:
  //   中断源
  //   时空图监测，可删除
  //   中断等待指示
  //   数码管输出
  //   控制位
  //   流水调试日志用
  //   暂停节拍，不能为0
  //   戳工具置1进入计数暂停模式，ctrl+k时钟自动运行到对应节拍暂停
  //   ctrl+k关闭时钟连续运行，将控制位置零，进入单步调试模式调试
  //   可计数暂停的时钟源
  //   为方便自动评测，需要输出流水线各段保存的PC值，注意是PC不是PC+4，另外ID段寄存器写入信息，Mem段内存写入信息也要输出
endmodule

module \中断按键参考电路  (
  input  \同步清零信号 ,
  output \与中断屏蔽位与 
);

  wire \_1号中断_out , and_1_out, clock_1_out, d_ff_1_q, or_1_out, or_2_out;

  Clock clock_1 (.out(clock_1_out));
  Button \_1号中断  (.out(\_1号中断_out ));
  LED \_1号中断等待指示灯  (.in(or_1_out));
  or or_1 (or_1_out, \与中断屏蔽位与 , d_ff_1_q);
  D_Flip_Flop #(.Pre_Clr_Positions("LEGACY"), .enable("true"), .NewFFLayout("false")) d_ff_1 (
    .clk(\_1号中断_out ), .D(1'b1), .Q(d_ff_1_q), .reset(\与中断屏蔽位与 ));  // open: Qn, preset, en
  or or_2 (or_2_out, d_ff_1_q, \与中断屏蔽位与 );
  and and_1 (and_1_out, or_2_out, ~\同步清零信号 );  // AND_Gate
  D_Flip_Flop #(.Pre_Clr_Positions("LEGACY"), .enable("true"), .NewFFLayout("false")) IR1 (
    .clk(clock_1_out), .D(and_1_out), .Q(\与中断屏蔽位与 ));  // open: Qn, preset, en, reset

  // Notes on the sheet:
  //   中断信号采样参考电路
  //   Reset 
endmodule

module \单周期_单级中断  (
  input  IR1,
  input  IR2,
  input  IR3,
  output RegWrite,
  output MemWrite,
  output [31:0] PC,
  output [31:0] IR,
  output [31:0] RDin,
  output [31:0] MDin,
  output [31:0] LedData
);

  wire CLK, clock_1_out, comparator_1_eq, comparator_2_eq, comparator_3_eq, comparator_4_eq, comparator_5_eq,
       comparator_5_lt, d_ff_1_q, Go, IR1_t, IR2_t, IR3_t, IRA, IRB, IRC, nand_1_out, or_1_out, W1, W2, W3;
  wire [12:0] CNT_num;
  wire [15:0] \总周期数 ;

  Button \u_继续运行  (.out(Go));
  Button _1 ();  // open: out
  Button _2 ();  // open: out
  Button _3 ();  // open: out
  LED led_1 (.in(W1));
  LED led_2 (.in(W2));
  LED led_3 (.in(W3));
  Hex_Digit_Display hex_digit_display_1 (.value(LedData[31:28]));  // open: dp
  Comparator #(.width(16)) comparator_1 (.a(16'h23b), .b(\总周期数 ), .eq(comparator_1_eq));  // open: gt, lt
  Comparator #(.width(16)) comparator_2 (.a(\总周期数 ), .b(16'h1), .eq(comparator_2_eq));  // open: gt, lt
  Comparator #(.width(16)) comparator_3 (.a(\总周期数 ), .b(16'h4), .eq(comparator_3_eq));  // open: gt, lt
  Comparator #(.width(16)) comparator_4 (.a(\总周期数 ), .b(16'h7), .eq(comparator_4_eq));  // open: gt, lt
  Hex_Digit_Display hex_digit_display_2 (.value(LedData[23:20]));  // open: dp
  Hex_Digit_Display hex_digit_display_3 (.value(LedData[27:24]));  // open: dp
  or or_1 (or_1_out, comparator_1_eq, comparator_2_eq);
  assign IRA = or_1_out ? ~CLK : 1'bz;  // Controlled_Inverter controlled_inverter_1
  assign IRB = comparator_3_eq ? ~CLK : 1'bz;  // Controlled_Inverter controlled_inverter_2
  assign IRC = comparator_4_eq ? ~CLK : 1'bz;  // Controlled_Inverter controlled_inverter_3
  Hex_Digit_Display hex_digit_display_4 (.value(LedData[15:12]));  // open: dp
  Hex_Digit_Display hex_digit_display_5 (.value(LedData[19:16]));  // open: dp
  Pull_Resistor pull_resistor_1 (.node(IRA));
  Pull_Resistor pull_resistor_2 (.node(IRB));
  Pull_Resistor pull_resistor_3 (.node(IRC));
  Hex_Digit_Display hex_digit_display_6 (.value(LedData[7:4]));  // open: dp
  Hex_Digit_Display hex_digit_display_7 (.value(LedData[11:8]));  // open: dp
  // Probe on \总周期数 
  Hex_Digit_Display hex_digit_display_8 (.value(LedData[3:0]));  // open: dp
  or or_2 (IR1_t, IR1, IRA);
  or or_3 (IR2_t, IR2, IRB);
  or or_4 (IR3_t, IR3, IRC);
  D_Flip_Flop #(.trigger("high"), .Pre_Clr_Positions("LEGACY"), .enable("true"), .NewFFLayout("false")) d_ff_1 (.Q(d_ff_1_q));  // open: clk, D, Qn, preset, en, reset
  // Probe on 13'hc
  Comparator #(.width(13)) comparator_5 (
    .a(CNT_num), .b(13'hc), .eq(comparator_5_eq), .lt(comparator_5_lt));  // open: gt
  Clock clock_1 (.out(clock_1_out));
  Counter #(.width(13), .max('h1fff), .ongoal("stay"), .behavior("old")) counter_1 (
    .count(comparator_5_lt), .Q(CNT_num), .clk(clock_1_out));  // open: load, D, carry, clr, preset
  nand nand_1 (nand_1_out, d_ff_1_q, comparator_5_eq);
  assign CLK = nand_1_out ? clock_1_out : 1'bz;  // Controlled_Buffer controlled_buffer_1
  Pull_Resistor #(.pull(1)) pull_resistor_4 (.node(CLK));

  // Notes on the sheet:
  //   中断源
  //   中断等待指示
  //   总复位信号应将除ROM以外所有存储组件全部清零
  //   单级中断测试信号模拟器
  //   数码管输出
  //   数码管输出应该用寄存器锁存，否则显示数据只能一闪而过
  //   为方便自动评测，需要输出PC，IR，寄存器堆写如数据RDin
  //   RAM写使能MemWrite、RAM写入数据MDin等信号
  //   控制位
  //   暂停节拍，不能为0
  //   戳工具置1进入计数暂停模式，ctrl+k时钟自动运行到对应节拍暂停
  //   ctrl+k关闭时钟连续运行，将控制位置零，进入单步调试模式调试
  //   可计数暂停的时钟源
endmodule

module \单周期_多级中断  (
  input  IR1,
  input  IR2,
  input  IR3,
  output RegWrite,
  output MemWrite,
  output [31:0] PC,
  output [31:0] IR,
  output [31:0] RDin,
  output [31:0] MDin,
  output [31:0] LedData
);

  wire CLK, clock_1_out, comparator_1_eq, comparator_2_eq, comparator_3_eq, comparator_4_eq, comparator_5_eq,
       comparator_6_eq, comparator_6_lt, d_ff_1_q, Go, IR1_t, IR2_t, IR3_t, IRA, IRB, IRC, nand_1_out,
       or_1_out, or_2_out, W1, W2, W3;
  wire [12:0] CNT_num;
  wire [15:0] \总周期数 ;

  Button \u_继续运行  (.out(Go));
  Button _1 ();  // open: out
  Button _2 ();  // open: out
  Button _3 ();  // open: out
  LED led_1 (.in(W1));
  LED led_2 (.in(W2));
  LED led_3 (.in(W3));
  Hex_Digit_Display hex_digit_display_1 (.value(LedData[31:28]));  // open: dp
  Comparator #(.width(16)) comparator_1 (.a(\总周期数 ), .b(16'h7), .eq(comparator_1_eq));  // open: gt, lt
  Comparator #(.width(16)) comparator_2 (.a(\总周期数 ), .b(16'h241), .eq(comparator_2_eq));  // open: gt, lt
  Hex_Digit_Display hex_digit_display_2 (.value(LedData[27:24]));  // open: dp
  Hex_Digit_Display hex_digit_display_3 (.value(LedData[23:20]));  // open: dp
  Comparator #(.width(16)) comparator_3 (.a(16'h258), .b(\总周期数 ), .eq(comparator_3_eq));  // open: gt, lt
  or or_1 (or_1_out, comparator_3_eq, comparator_4_eq);
  Comparator #(.width(16)) comparator_4 (.a(\总周期数 ), .b(16'h1), .eq(comparator_4_eq));  // open: gt, lt
  Comparator #(.width(16)) comparator_5 (.a(\总周期数 ), .b(16'h4), .eq(comparator_5_eq));  // open: gt, lt
  or or_2 (or_2_out, comparator_1_eq, comparator_2_eq);
  Hex_Digit_Display hex_digit_display_4 (.value(LedData[15:12]));  // open: dp
  Hex_Digit_Display hex_digit_display_5 (.value(LedData[19:16]));  // open: dp
  Pull_Resistor pull_resistor_1 (.node(IRA));
  assign IRA = or_1_out ? ~CLK : 1'bz;  // Controlled_Inverter controlled_inverter_1
  Pull_Resistor pull_resistor_2 (.node(IRB));
  assign IRB = comparator_5_eq ? ~CLK : 1'bz;  // Controlled_Inverter controlled_inverter_2
  Pull_Resistor pull_resistor_3 (.node(IRC));
  assign IRC = or_2_out ? ~CLK : 1'bz;  // Controlled_Inverter controlled_inverter_3
  Hex_Digit_Display hex_digit_display_6 (.value(LedData[11:8]));  // open: dp
  Hex_Digit_Display hex_digit_display_7 (.value(LedData[7:4]));  // open: dp
  // Probe on \总周期数 
  Hex_Digit_Display hex_digit_display_8 (.value(LedData[3:0]));  // open: dp
  or or_3 (IR1_t, IR1, IRA);
  or or_4 (IR2_t, IR2, IRB);
  or or_5 (IR3_t, IR3, IRC);
  D_Flip_Flop #(.trigger("high"), .Pre_Clr_Positions("LEGACY"), .enable("true"), .NewFFLayout("false")) d_ff_1 (.Q(d_ff_1_q));  // open: clk, D, Qn, preset, en, reset
  // Probe on 13'hc
  Comparator #(.width(13)) comparator_6 (
    .a(CNT_num), .b(13'hc), .eq(comparator_6_eq), .lt(comparator_6_lt));  // open: gt
  Clock clock_1 (.out(clock_1_out));
  Counter #(.width(13), .max('h1fff), .ongoal("stay"), .behavior("old")) counter_1 (
    .count(comparator_6_lt), .Q(CNT_num), .clk(clock_1_out));  // open: load, D, carry, clr, preset
  nand nand_1 (nand_1_out, d_ff_1_q, comparator_6_eq);
  assign CLK = nand_1_out ? clock_1_out : 1'bz;  // Controlled_Buffer controlled_buffer_1
  Pull_Resistor #(.pull(1)) pull_resistor_4 (.node(CLK));

  // Notes on the sheet:
  //   中断源
  //   中断等待指示
  //   总复位信号应将除ROM以外所有存储组件全部清零
  //   多级中断测试信号模拟器
  //   数码管输出
  //   数码管输出应该用寄存器锁存，否则显示数据只能一闪而过
  //   为方便自动评测，需要输出PC，IR，寄存器堆写如数据RDin
  //   RAM写使能MemWrite、RAM写入数据MDin等信号
  //   控制位
  //   暂停节拍，不能为0
  //   戳工具置1进入计数暂停模式，ctrl+k时钟自动运行到对应节拍暂停
  //   ctrl+k关闭时钟连续运行，将控制位置零，进入单步调试模式调试
  //   可计数暂停的时钟源
endmodule

module \封装正确性测试  (
);

  wire IR1, IR2, IR3, MemW, RegW;
  wire [31:0] EX_PC, ID_PC, IF_PC, IR, LED, MDin, MDinr, MEM_PC, PC, RDin, RDinr, WB_PC;

  \单周期RISC_V  \u_单周期risc_v_1  (
    .IR1(IR1), .IR2(IR2), .IR3(IR3), .RegWrite(RegW), .MemWrite(MemW), .PC(PC), .IR(IR), .RDin(RDin),
    .MDin(MDin), .LedData(LED));
  \气泡流水线  \u_气泡流水线_1  (
    .RegWrite(RegW), .MemWrite(MemW), .IF_PC(IF_PC), .ID_PC(ID_PC), .EX_PC(EX_PC), .M_PC(MEM_PC),
    .WB_PC(WB_PC), .RDin(RDinr), .MDin(MDinr), .LedData(LED));
  \单周期_单级中断  \u_单周期_单级中断_1  (
    .IR1(IR1), .IR2(IR2), .IR3(IR3), .RegWrite(RegW), .MemWrite(MemW), .PC(PC), .IR(IR), .RDin(RDin),
    .MDin(MDin), .LedData(LED));
  \理想流水线  \u_理想流水线_1  (
    .RegWrite(RegW), .MemWrite(MemW), .IF_PC(IF_PC), .ID_PC(ID_PC), .EX_PC(EX_PC), .M_PC(MEM_PC),
    .WB_PC(WB_PC), .RDin(RDinr), .MDin(MDinr), .LedData(LED));
  \重定向流水线  \u_重定向流水线_1  (
    .RegWrite(RegW), .MemWrite(MemW), .IF_PC(IF_PC), .ID_PC(ID_PC), .EX_PC(EX_PC), .M_PC(MEM_PC),
    .WB_PC(WB_PC), .RDin(RDinr), .MDin(MDinr), .LedData(LED));
  \单周期_多级中断  \u_单周期_多级中断_1  (
    .IR1(IR1), .IR2(IR2), .IR3(IR3), .RegWrite(RegW), .MemWrite(MemW), .PC(PC), .IR(IR), .RDin(RDin),
    .MDin(MDin), .LedData(LED));

  // Notes on the sheet:
  //   单周期封装测试
  //   气泡流水封装测试
  //   单周期+单级中断封装测试
  //   请检查上面封装有无位宽不匹配，引脚标签是否和连接的标签相对应，否则无法在educoder平台上正确测试
  //   理想流水封装测试
  //   重定向流水封装测试
  //   单周期+多级中断封装测试
endmodule

module IF_ID (
  input  [31:0] IRin,
  input  [31:0] PCin,
  input  CLK,
  input  RST,
  output [31:0] IRout,
  output [31:0] PCout
);

  Register #(.width(32), .Select("low")) register_1 (.D(IRin), .Q(IRout), .clk(CLK), .clr(RST));  // open: en
  Register #(.width(32), .Select("low")) register_2 (.D(PCin), .Q(PCout), .clk(CLK), .clr(RST));  // open: en
endmodule

module ID_EX (
  input  Bytein,
  input  BGEin,
  input  URETin,
  input  JALRin,
  input  JALin,
  input  BEQin,
  input  MemToRegin,
  input  MemWritein,
  input  [3:0] AluOPin,
  input  AluSrcBin,
  input  RegWritein,
  input  UTypein,
  input  [31:0] R1in,
  input  [31:0] R2in,
  input  [4:0] RTagin,
  input  [31:0] Immin,
  input  [31:0] PCin,
  input  BNEin,
  input  CLK,
  input  RST,
  output Byteout,
  output BGEout,
  output URETout,
  output JALRout,
  output JALout,
  output BEQout,
  output MemToRegout,
  output MemWriteout,
  output [3:0] AluOPout,
  output AluSrcBout,
  output RegWriteout,
  output UTypeout,
  output [31:0] R1out,
  output [31:0] R2out,
  output [4:0] RTagout,
  output [31:0] Immout,
  output [31:0] PCout,
  output BNEout
);

  Register #(.width(1), .Select("low")) register_1 (.D(Bytein), .Q(Byteout), .clk(CLK), .clr(RST));  // open: en
  Register #(.width(1), .Select("low")) register_2 (.D(BGEin), .Q(BGEout), .clk(CLK), .clr(RST));  // open: en
  Register #(.width(1), .Select("low")) register_3 (.D(URETin), .Q(URETout), .clk(CLK), .clr(RST));  // open: en
  Register #(.width(1), .Select("low")) register_4 (.D(JALRin), .Q(JALRout), .clk(CLK), .clr(RST));  // open: en
  Register #(.width(1), .Select("low")) register_5 (.D(JALin), .Q(JALout), .clk(CLK), .clr(RST));  // open: en
  Register #(.width(1), .Select("low")) register_6 (.D(BEQin), .Q(BEQout), .clk(CLK), .clr(RST));  // open: en
  Register #(.width(1), .Select("low")) register_7 (.D(MemToRegin), .Q(MemToRegout), .clk(CLK), .clr(RST));  // open: en
  Register #(.width(1), .Select("low")) register_8 (.D(MemWritein), .Q(MemWriteout), .clk(CLK), .clr(RST));  // open: en
  Register #(.width(4), .Select("low")) register_9 (.D(AluOPin), .Q(AluOPout), .clk(CLK), .clr(RST));  // open: en
  Register #(.width(1), .Select("low")) register_10 (.D(AluSrcBin), .Q(AluSrcBout), .clk(CLK), .clr(RST));  // open: en
  Register #(.width(1), .Select("low")) register_11 (
    .D(RegWritein), .Q(RegWriteout), .clk(CLK), .clr(RST));  // open: en
  Register #(.width(1), .Select("low")) register_12 (.D(UTypein), .Q(UTypeout), .clk(CLK), .clr(RST));  // open: en
  Register #(.width(32), .Select("low")) register_13 (.D(R1in), .Q(R1out), .clk(CLK), .clr(RST));  // open: en
  Register #(.width(32), .Select("low")) register_14 (.D(R2in), .Q(R2out), .clk(CLK), .clr(RST));  // open: en
  Register #(.width(5), .Select("low")) register_15 (.D(RTagin), .Q(RTagout), .clk(CLK), .clr(RST));  // open: en
  Register #(.width(32), .Select("low")) register_16 (.D(Immin), .Q(Immout), .clk(CLK), .clr(RST));  // open: en
  Register #(.width(32), .Select("low")) register_17 (.D(PCin), .Q(PCout), .clk(CLK), .clr(RST));  // open: en
  Register #(.width(1), .Select("low")) register_18 (.D(BNEin), .Q(BNEout), .clk(CLK), .clr(RST));  // open: en
endmodule

module EX_MEM (
  input  Bytein,
  input  MemToRegin,
  input  MemWritein,
  input  JALRin,
  input  JALin,
  input  RegWritein,
  input  UTypein,
  input  [31:0] PCin,
  input  [31:0] Resultin,
  input  [4:0] RTagin,
  input  [31:0] Immin,
  input  CLK,
  input  RST,
  output Byteout,
  output MemToRegout,
  output MemWriteout,
  output JALRout,
  output JALout,
  output RegWriteout,
  output UTypeout,
  output [31:0] PCout,
  output [31:0] Resultout,
  output [4:0] RTagout,
  output [31:0] Immout
);

  Register #(.width(1), .Select("low")) register_1 (.D(Bytein), .Q(Byteout), .clk(CLK), .clr(RST));  // open: en
  Register #(.width(1), .Select("low")) register_2 (.D(MemToRegin), .Q(MemToRegout), .clk(CLK), .clr(RST));  // open: en
  Register #(.width(1), .Select("low")) register_3 (.D(MemWritein), .Q(MemWriteout), .clk(CLK), .clr(RST));  // open: en
  Register #(.width(1), .Select("low")) register_4 (.D(JALRin), .Q(JALRout), .clk(CLK), .clr(RST));  // open: en
  Register #(.width(1), .Select("low")) register_5 (.D(JALin), .Q(JALout), .clk(CLK), .clr(RST));  // open: en
  Register #(.width(1), .Select("low")) register_6 (.D(RegWritein), .Q(RegWriteout), .clk(CLK), .clr(RST));  // open: en
  Register #(.width(1), .Select("low")) register_7 (.D(UTypein), .Q(UTypeout), .clk(CLK), .clr(RST));  // open: en
  Register #(.width(32), .Select("low")) register_8 (.D(PCin), .Q(PCout), .clk(CLK), .clr(RST));  // open: en
  Register #(.width(32), .Select("low")) register_9 (.D(Resultin), .Q(Resultout), .clk(CLK), .clr(RST));  // open: en
  Register #(.width(5), .Select("low")) register_10 (.D(RTagin), .Q(RTagout), .clk(CLK), .clr(RST));  // open: en
  Register #(.width(32), .Select("low")) register_11 (.D(Immin), .Q(Immout), .clk(CLK), .clr(RST));  // open: en
endmodule

module MEM_WB (
  input  RegWritein,
  input  [31:0] WriteDatain,
  input  [4:0] RTagin,
  input  [31:0] PCin,
  input  CLK,
  input  RST,
  output RegWriteout,
  output [31:0] WriteDataout,
  output [4:0] RTagout,
  output [31:0] PCout
);

  Register #(.width(1), .Select("low")) register_1 (.D(RegWritein), .Q(RegWriteout), .clk(CLK), .clr(RST));  // open: en
  Register #(.width(32), .Select("low")) register_2 (
    .D(WriteDatain), .Q(WriteDataout), .clk(CLK), .clr(RST));  // open: en
  Register #(.width(5), .Select("low")) register_3 (.D(RTagin), .Q(RTagout), .clk(CLK), .clr(RST));  // open: en
  Register #(.width(32), .Select("low")) register_4 (.D(PCin), .Q(PCout), .clk(CLK), .clr(RST));  // open: en
endmodule

module \立即数类别识别  (
  input  OP2,
  input  OP3,
  input  OP4,
  input  OP5,
  input  OP6,
  input  F12,
  input  F13,
  input  F14,
  input  F25,
  input  F30,
  output I,
  output S,
  output B,
  output J,
  output U
);

  wire and_1_out, and_2_out, and_3_out, and_4_out, and_5_out, and_6_out, and_7_out, and_8_out, and_9_out,
       and_10_out, and_11_out, and_12_out, and_14_out, and_15_out, and_16_out, and_17_out, and_18_out,
       not_1_out, not_2_out, not_3_out, not_4_out, not_5_out, not_6_out, not_7_out, not_8_out, not_9_out,
       not_10_out, not_11_out, not_12_out, not_13_out, not_14_out, not_15_out, not_16_out, not_17_out,
       not_18_out, not_19_out, not_20_out, not_21_out, not_22_out, not_23_out, not_24_out, not_25_out,
       not_26_out, not_27_out, not_28_out, not_29_out, not_30_out, not_31_out, not_32_out, not_33_out,
       not_34_out, not_35_out, not_36_out, not_37_out, not_38_out, not_39_out, not_40_out, not_41_out,
       not_42_out, not_43_out, not_44_out, not_45_out, not_46_out, not_47_out, not_48_out, not_49_out,
       not_50_out, not_51_out, not_52_out, not_53_out, not_54_out, not_55_out, not_56_out, not_57_out,
       not_58_out, not_59_out, not_60_out, not_61_out, not_62_out, not_63_out, not_64_out, not_65_out,
       not_66_out, not_67_out, not_68_out, not_69_out, not_70_out, not_71_out, not_72_out, not_73_out,
       not_74_out, not_75_out, not_76_out, not_77_out, not_78_out, not_79_out, not_80_out, not_81_out,
       not_82_out, not_83_out, not_84_out, not_85_out, not_86_out, not_87_out, not_88_out, not_89_out,
       not_90_out, not_91_out, not_92_out, not_93_out, not_94_out;

  not not_1 (not_1_out, F14);
  not not_2 (not_2_out, F13);
  not not_3 (not_3_out, F12);
  not not_4 (not_4_out, OP6);
  not not_5 (not_5_out, OP5);
  not not_6 (not_6_out, OP3);
  not not_7 (not_7_out, OP2);
  not not_8 (not_8_out, OP6);
  not not_9 (not_9_out, OP5);
  not not_10 (not_10_out, OP3);
  not not_11 (not_11_out, OP2);
  not not_12 (not_12_out, F12);
  not not_13 (not_13_out, OP6);
  not not_14 (not_14_out, OP5);
  not not_15 (not_15_out, OP3);
  not not_16 (not_16_out, OP2);
  not not_17 (not_17_out, F13);
  not not_18 (not_18_out, F12);
  not not_19 (not_19_out, OP6);
  not not_20 (not_20_out, OP5);
  not not_21 (not_21_out, OP3);
  not not_22 (not_22_out, OP2);
  not not_23 (not_23_out, F14);
  not not_24 (not_24_out, F12);
  not not_25 (not_25_out, OP6);
  not not_26 (not_26_out, OP5);
  not not_27 (not_27_out, OP3);
  not not_28 (not_28_out, OP2);
  not not_29 (not_29_out, F30);
  not not_30 (not_30_out, F25);
  not not_31 (not_31_out, F14);
  not not_32 (not_32_out, F13);
  not not_33 (not_33_out, OP6);
  not not_34 (not_34_out, OP5);
  not not_35 (not_35_out, OP3);
  not not_36 (not_36_out, OP2);
  not not_37 (not_37_out, F30);
  not not_38 (not_38_out, F25);
  not not_39 (not_39_out, F13);
  not not_40 (not_40_out, OP6);
  not not_41 (not_41_out, OP5);
  not not_42 (not_42_out, OP3);
  not not_43 (not_43_out, OP2);
  not not_44 (not_44_out, F25);
  not not_45 (not_45_out, F13);
  not not_46 (not_46_out, OP6);
  not not_47 (not_47_out, OP5);
  not not_48 (not_48_out, OP3);
  not not_49 (not_49_out, OP2);
  not not_50 (not_50_out, F14);
  not not_51 (not_51_out, F12);
  not not_52 (not_52_out, OP6);
  not not_53 (not_53_out, OP5);
  not not_54 (not_54_out, OP4);
  not not_55 (not_55_out, OP3);
  not not_56 (not_56_out, OP2);
  not not_57 (not_57_out, F12);
  not not_58 (not_58_out, OP3);
  not not_59 (not_59_out, OP2);
  not not_60 (not_60_out, OP3);
  not not_61 (not_61_out, OP2);
  not not_62 (not_62_out, F13);
  not not_63 (not_63_out, F12);
  not not_64 (not_64_out, OP6);
  not not_65 (not_65_out, OP5);
  not not_66 (not_66_out, OP4);
  not not_67 (not_67_out, OP3);
  not not_68 (not_68_out, OP2);
  not not_69 (not_69_out, F14);
  not not_70 (not_70_out, F12);
  not not_71 (not_71_out, OP6);
  not not_72 (not_72_out, OP4);
  not not_73 (not_73_out, OP3);
  not not_74 (not_74_out, OP2);
  not not_75 (not_75_out, F14);
  not not_76 (not_76_out, F13);
  not not_77 (not_77_out, F12);
  not not_78 (not_78_out, OP4);
  not not_79 (not_79_out, OP3);
  not not_80 (not_80_out, OP2);
  not not_81 (not_81_out, F14);
  not not_82 (not_82_out, F13);
  not not_83 (not_83_out, OP4);
  not not_84 (not_84_out, OP3);
  not not_85 (not_85_out, OP2);
  not not_86 (not_86_out, F13);
  not not_87 (not_87_out, OP4);
  not not_88 (not_88_out, OP3);
  not not_89 (not_89_out, OP2);
  not not_90 (not_90_out, OP4);
  not not_91 (not_91_out, OP4);
  not not_92 (not_92_out, OP3);
  not not_93 (not_93_out, OP6);
  not not_94 (not_94_out, OP3);
  and and_1 (and_1_out, not_1_out, not_2_out, not_3_out, not_4_out, not_5_out, OP4, not_6_out, not_7_out);
  and and_2 (and_2_out, F14, F13, F12, not_8_out, not_9_out, OP4, not_10_out, not_11_out);
  and and_3 (and_3_out, F14, F13, not_12_out, not_13_out, not_14_out, OP4, not_15_out, not_16_out);
  and and_4 (and_4_out, F14, not_17_out, not_18_out, not_19_out, not_20_out, OP4, not_21_out, not_22_out);
  and and_5 (and_5_out, not_23_out, F13, not_24_out, not_25_out, not_26_out, OP4, not_27_out, not_28_out);
  and and_6 (and_6_out, not_29_out, not_30_out, not_31_out, not_32_out, F12, not_33_out, not_34_out, OP4, not_35_out, not_36_out);
  and and_7 (and_7_out, not_37_out, not_38_out, F14, not_39_out, F12, not_40_out, not_41_out, OP4, not_42_out, not_43_out);
  and and_8 (and_8_out, F30, not_44_out, F14, not_45_out, F12, not_46_out, not_47_out, OP4, not_48_out, not_49_out);
  and and_9 (and_9_out, not_50_out, F13, not_51_out, not_52_out, not_53_out, not_54_out, not_55_out, not_56_out);
  and and_10 (and_10_out, F14, F13, not_57_out, OP6, OP5, OP4, not_58_out, not_59_out);
  and and_11 (and_11_out, F14, F13, F12, OP6, OP5, OP4, not_60_out, not_61_out);
  and and_12 (and_12_out, F14, not_62_out, not_63_out, not_64_out, not_65_out, not_66_out, not_67_out, not_68_out);
  and and_13 (S, not_69_out, F13, not_70_out, not_71_out, OP5, not_72_out, not_73_out, not_74_out);
  and and_14 (and_14_out, not_75_out, not_76_out, not_77_out, OP6, OP5, not_78_out, not_79_out, not_80_out);
  and and_15 (and_15_out, not_81_out, not_82_out, F12, OP6, OP5, not_83_out, not_84_out, not_85_out);
  and and_16 (and_16_out, F14, not_86_out, F12, OP6, OP5, not_87_out, not_88_out, not_89_out);
  and and_17 (and_17_out, OP6, OP5, not_90_out, OP3, OP2);
  and and_18 (and_18_out, OP6, OP5, not_91_out, not_92_out, OP2);
  and and_19 (U, not_93_out, OP5, OP4, not_94_out, OP2);
  or or_1 (B, and_14_out, and_15_out, and_16_out);
  or or_2 (J, and_17_out, and_18_out);
  or or_3 (I, and_1_out, and_2_out, and_3_out, and_4_out, and_5_out, and_6_out, and_7_out, and_8_out, and_9_out, and_10_out, and_11_out, and_12_out);
endmodule

module \立即数类型识别器  (
  input  [4:0] OP,
  input  [4:0] Funct,
  output I,
  output S,
  output B,
  output J,
  output U
);

  \立即数类别识别  \u_立即数类别识别_1  (
    .OP2(OP[0]), .OP3(OP[1]), .OP4(OP[2]), .OP5(OP[3]), .OP6(OP[4]), .F12(Funct[0]), .F13(Funct[1]),
    .F14(Funct[2]), .F25(Funct[3]), .F30(Funct[4]), .I(I), .S(S), .B(B), .J(J), .U(U));
endmodule
